// Logisim project 1.circ as structural Verilog: 16 circuits, main circuit 四位二进制可逆计数器
module \四位二进制可逆计数器  (
  input  CLR,
  input  CPU,
  input  CPD,
  output Q1,
  output Q2,
  output Q3,
  output Q4,
  output out_8,
  output out_9
);

  wire and_1_out, and_2_out, and_6_out, and_7_out, and_8_out, and_9_out, and_10_out, CP, nand_1_out,
       not_1_out, or_1_out, or_3_out, or_4_out, or_5_out, x, x_minus, xor_1_out, xor_2_out, xor_3_out,
       xor_4_out, y1_minus, y2_minus, y3_minus, y4_minus;

  not not_1 (not_1_out, CPD);
  and and_1 (and_1_out, y1_minus, y2_minus, y3_minus, x_minus);
  and and_2 (and_2_out, y3_minus, Q2, Q1, x);
  xor xor_1 (xor_1_out, Q2, Q1);
  or or_1 (or_1_out, xor_1_out, xor_2_out);
  xor xor_2 (xor_2_out, Q2, x);
  or or_2 (CP, CPU, CPD);
  and and_3 (x, CPU, not_1_out);
  not not_2 (x_minus, x);
  and and_4 (out_8, x, Q1, Q2, Q3, Q4);
  and and_5 (out_9, CPD, ~Q1, ~Q2, ~Q3, ~Q4);  // AND_Gate
  or or_3 (or_3_out, and_1_out, and_2_out, and_6_out);
  and and_6 (and_6_out, Q3, or_1_out);
  D_Flip_Flop #(.trigger("falling")) Y3 (
    .clk(CP), .D(or_3_out), .Q(Q3), .Qn(y3_minus), .reset(CLR));  // open: preset, en
  xor xor_3 (xor_3_out, x_minus, Q1);
  and and_7 (and_7_out, y4_minus, Q3, Q1, Q2, x);
  and and_8 (and_8_out, y4_minus, y3_minus, y1_minus, y2_minus, x_minus);
  xor xor_4 (xor_4_out, xor_3_out, Q2);
  and and_9 (and_9_out, Q4, x_minus, or_4_out);
  or or_4 (or_4_out, Q1, Q2, Q3);
  and and_10 (and_10_out, Q4, x, nand_1_out);
  nand nand_1 (nand_1_out, Q1, Q2, Q3);
  D_Flip_Flop #(.trigger("falling")) Y1 (
    .clk(CP), .D(y1_minus), .Q(Q1), .Qn(y1_minus), .reset(CLR));  // open: preset, en
  D_Flip_Flop #(.trigger("falling")) Y2 (
    .clk(CP), .D(xor_4_out), .Q(Q2), .Qn(y2_minus), .reset(CLR));  // open: preset, en
  D_Flip_Flop #(.trigger("falling")) Y4 (
    .clk(CP), .D(or_5_out), .Q(Q4), .Qn(y4_minus), .reset(CLR));  // open: preset, en
  or or_5 (or_5_out, and_7_out, and_8_out, and_9_out, and_10_out);

  // Other names for the same wires on the sheet: y1 = Q1; y2 = Q2; y3 = Q3; y4 = Q4
endmodule

module \test四位二进制可逆计数器  (
  input  in_1,
  output out_2,
  output out_3,
  output out_4,
  output out_5
);

  wire CLR_out, CPD_out, CPU_out;

  Button CPU (.out(CPU_out));
  Button CLR (.out(CLR_out));
  Button CPD (.out(CPD_out));
  // 四位二进制可逆计数器 四位二进制可逆计数器_1: pin names not known; wires that end beside it: CPU_out, CLR_out, CPD_out, out_2, out_3, out_4, in_1, out_5
endmodule

module \二进制转换为BCD码  (
  input  A2,
  input  A1,
  input  A3,
  input  in_4,
  output x3,
  output x2,
  output x1,
  output x0,
  output y3,
  output y2,
  output y1,
  output y0
);

  wire and_2_out, or_1_out;

  or or_1 (or_1_out, A2, A1);
  and and_1 (y0, or_1_out, A3);
  and and_2 (and_2_out, 1'b1, y0);
  \先行进位四位二进制加法器  \u_先行进位四位二进制加法器_1  (
    .A0(in_4), .B0(and_2_out), .A1(A1), .B1(1'b0), .A2(A2), .B2(and_2_out), .A3(A3), .B3(1'b0), .S0(x0),
    .S1(x1), .S2(x2), .S3(x3), .C0(y0));  // open: C4

  assign y1 = 1'b0;
  assign y2 = 1'b0;
  assign y3 = 1'b0;
endmodule

module \test二进制转换为BCD码  (
  input  A3,
  input  A2,
  input  A1,
  input  A0,
  output out_5,
  output out_6,
  output out_7,
  output out_8,
  output out_9,
  output out_10,
  output out_11,
  output out_12
);

  \二进制转换为BCD码  \u_二进制转换为bcd码_1  (
    .A2(A2), .A1(A1), .A3(A3), .x3(out_9), .x2(out_10), .x1(out_11), .x0(out_12), .y3(out_5), .y2(out_6),
    .in_4(A0), .y1(out_7), .y0(out_8));
endmodule

module \译码器电路  (
  input  x3,
  input  x2,
  input  x1,
  input  x0,
  output y3,
  output y2,
  output y1,
  output y0,
  output y6,
  output y5,
  output y4
);

  wire not_1_out, not_2_out, not_3_out, x1_x0_minus_out, x1x0_minus_out, x1x0_out, x2_x0_minus_out,
       x2_x1_out, x2x0_minus_out, x2x0_out, x2x1_minus_out, x2x1_x0_out, x3x0_minus_out;

  not not_1 (not_1_out, x2);
  not not_2 (not_2_out, x1);
  not not_3 (not_3_out, x0);
  or or_1 (y6, x3, x2, not_2_out, x0);
  and x2_x1 (x2_x1_out, not_1_out, x1);
  and x2x1_x0 (x2x1_x0_out, x2, not_2_out, x0);
  and x2_x0_minus (x2_x0_minus_out, not_1_out, not_3_out);
  and x1x0_minus (x1x0_minus_out, x1, not_3_out);
  and x3x0_minus (x3x0_minus_out, not_3_out, x3);
  and x1x0 (x1x0_out, x1, x0);
  and x1_x0_minus (x1_x0_minus_out, not_2_out, not_3_out);
  and x2x0 (x2x0_out, x2, x0);
  and x2x0_minus (x2x0_minus_out, x2, not_3_out);
  and x2x1_minus (x2x1_minus_out, x2, not_2_out);
  or or_2 (y5, x2_x1_out, x2x1_x0_out, x2_x0_minus_out, x1x0_minus_out, x3);
  or or_3 (y4, x1x0_minus_out, x2_x0_minus_out, x3x0_minus_out);
  or or_4 (y3, not_1_out, x1x0_out, x2_x1_out, x1_x0_minus_out, x3);
  or or_5 (y2, x1, x2x0_out, x2_x0_minus_out, x3);
  or or_6 (y1, x2x0_minus_out, x2x1_minus_out, x1_x0_minus_out, x3);
  or or_7 (y0, x2_x1_out, x2x1_minus_out, x2x0_minus_out, x3);
endmodule

module \test译码器电路  (
  input  A3,
  input  A2,
  input  A1,
  input  A0
);

  wire \译码器电路_1_y0 , \译码器电路_1_y1 , \译码器电路_1_y2 , \译码器电路_1_y3 , \译码器电路_1_y4 , \译码器电路_1_y5 , \译码器电路_1_y6 ;

  \译码器电路  \u_译码器电路_1  (
    .x3(A3), .x2(A2), .x1(A1), .x0(A0), .y3(\译码器电路_1_y3 ), .y2(\译码器电路_1_y2 ), .y1(\译码器电路_1_y1 ),
    .y0(\译码器电路_1_y0 ), .y6(\译码器电路_1_y6 ), .y5(\译码器电路_1_y5 ), .y4(\译码器电路_1_y4 ));
  _7_Segment_Display u_7_segment_display_1 (
    .g(\译码器电路_1_y0 ), .f(\译码器电路_1_y1 ), .a(\译码器电路_1_y2 ), .b(\译码器电路_1_y3 ), .e(\译码器电路_1_y4 ),
    .d(\译码器电路_1_y5 ), .c(\译码器电路_1_y6 ));  // open: dp
endmodule

module \小型门禁  (
  input  CPU,
  input  CLR,
  input  CPD,
  output out_4,
  output g1,
  output g2,
  output f1,
  output f2,
  output e1,
  output e2,
  output d1,
  output d2,
  output c1,
  output c2,
  output b1,
  output b2,
  output a1,
  output a2
);

  wire and_1_out, and_2_out, nand_1_out, or_1_out, \二进制转换为bcd码_1_x0 , \二进制转换为bcd码_1_x1 , \二进制转换为bcd码_1_x2 ,
       \二进制转换为bcd码_1_x3 , \二进制转换为bcd码_1_y0 , \二进制转换为bcd码_1_y1 , \二进制转换为bcd码_1_y2 , \二进制转换为bcd码_1_y3 ,
       \四位二进制可逆计数器_1_p4 , \四位二进制可逆计数器_1_p5 , \四位二进制可逆计数器_1_p6 , \四位二进制可逆计数器_1_p7 ;

  \报警电路  \u_报警电路_1  (.in_1(CPU), .in_2(CLR), .in_3(CPD), .out_4(out_4));
  nand nand_1 (nand_1_out, \四位二进制可逆计数器_1_p7 , \四位二进制可逆计数器_1_p6 , \四位二进制可逆计数器_1_p5 , \四位二进制可逆计数器_1_p4 );
  or or_1 (or_1_out, \四位二进制可逆计数器_1_p7 , \四位二进制可逆计数器_1_p6 , \四位二进制可逆计数器_1_p5 , \四位二进制可逆计数器_1_p4 );
  and and_1 (and_1_out, nand_1_out, CPU);
  and and_2 (and_2_out, or_1_out, CPD);
  \二进制转换为BCD码  \u_二进制转换为bcd码_1  (
    .A2(\四位二进制可逆计数器_1_p5 ), .A1(\四位二进制可逆计数器_1_p6 ), .A3(\四位二进制可逆计数器_1_p4 ), .x3(\二进制转换为bcd码_1_x3 ),
    .x2(\二进制转换为bcd码_1_x2 ), .x1(\二进制转换为bcd码_1_x1 ), .x0(\二进制转换为bcd码_1_x0 ), .y3(\二进制转换为bcd码_1_y3 ),
    .y2(\二进制转换为bcd码_1_y2 ), .in_4(\四位二进制可逆计数器_1_p7 ), .y1(\二进制转换为bcd码_1_y1 ), .y0(\二进制转换为bcd码_1_y0 ));
  // 四位二进制可逆计数器 四位二进制可逆计数器_1: pin names not known; wires that end beside it: and_1_out, CLR, and_2_out, \四位二进制可逆计数器_1_p4 , \四位二进制可逆计数器_1_p5 , \四位二进制可逆计数器_1_p6 , \四位二进制可逆计数器_1_p7 
  \译码器电路  \u_译码器电路_1  (
    .x3(\二进制转换为bcd码_1_x3 ), .x2(\二进制转换为bcd码_1_x2 ), .x1(\二进制转换为bcd码_1_x1 ), .x0(\二进制转换为bcd码_1_x0 ), .y3(d1),
    .y2(c1), .y1(b1), .y0(a1), .y6(g1), .y5(f1), .y4(e1));
  \译码器电路  \u_译码器电路_2  (
    .x3(\二进制转换为bcd码_1_y3 ), .x2(\二进制转换为bcd码_1_y2 ), .x1(\二进制转换为bcd码_1_y1 ), .x0(\二进制转换为bcd码_1_y0 ), .y3(d2),
    .y2(c2), .y1(b2), .y0(a2), .y6(g2), .y5(f2), .y4(e2));
endmodule

module \test报警电路  (
  output out_1,
  output out_2,
  output out_3,
  output out_4
);

  wire and_1_out, and_2_out, CLR_out, CPD_out, CPU_out, nand_1_out, or_1_out, \报警电路_1_out_4 ;

  Button CPU (.out(CPU_out));
  Button CPD (.out(CPD_out));
  LED led_1 (.in(\报警电路_1_out_4 ));
  \报警电路  \u_报警电路_1  (.in_1(CPU_out), .in_2(CLR_out), .in_3(CPD_out), .out_4(\报警电路_1_out_4 ));
  nand nand_1 (nand_1_out, out_4, out_3, out_2, out_1);
  or or_1 (or_1_out, out_4, out_3, out_2, out_1);
  and and_1 (and_1_out, nand_1_out, CPU_out);
  Button CLR (.out(CLR_out));
  and and_2 (and_2_out, or_1_out, CPD_out);
  // 四位二进制可逆计数器 四位二进制可逆计数器_1: pin names not known; wires that end beside it: and_1_out, CLR_out, and_2_out, out_1, out_2, out_3, out_4
endmodule

module \报警电路  (
  input  in_1,
  input  in_2,
  input  in_3,
  output out_4
);

  wire and_2_out, and_3_out, nand_1_out, or_1_out, \四位二进制可逆计数器_1_p4 , \四位二进制可逆计数器_1_p5 , \四位二进制可逆计数器_1_p6 ,
       \四位二进制可逆计数器_1_p7 ;

  and and_1 (out_4, in_1, \四位二进制可逆计数器_1_p7 , \四位二进制可逆计数器_1_p6 , \四位二进制可逆计数器_1_p5 , \四位二进制可逆计数器_1_p4 );
  nand nand_1 (nand_1_out, \四位二进制可逆计数器_1_p7 , \四位二进制可逆计数器_1_p6 , \四位二进制可逆计数器_1_p5 , \四位二进制可逆计数器_1_p4 );
  or or_1 (or_1_out, \四位二进制可逆计数器_1_p7 , \四位二进制可逆计数器_1_p6 , \四位二进制可逆计数器_1_p5 , \四位二进制可逆计数器_1_p4 );
  and and_2 (and_2_out, nand_1_out, in_1);
  and and_3 (and_3_out, or_1_out, in_3);
  // 四位二进制可逆计数器 四位二进制可逆计数器_1: pin names not known; wires that end beside it: and_2_out, in_2, and_3_out, \四位二进制可逆计数器_1_p4 , \四位二进制可逆计数器_1_p5 , \四位二进制可逆计数器_1_p6 , \四位二进制可逆计数器_1_p7 
endmodule

module \test门禁电路  (
);

  wire CLR_out, CPD_out, CPU_out, \小型门禁_1_a1 , \小型门禁_1_a2 , \小型门禁_1_b1 , \小型门禁_1_b2 , \小型门禁_1_c1 ,
       \小型门禁_1_c2 , \小型门禁_1_d1 , \小型门禁_1_d2 , \小型门禁_1_e1 , \小型门禁_1_e2 , \小型门禁_1_f1 , \小型门禁_1_f2 ,
       \小型门禁_1_g1 , \小型门禁_1_g2 , \小型门禁_1_out_4 ;

  Button CPU (.out(CPU_out));
  Button CPD (.out(CPD_out));
  Button CLR (.out(CLR_out));
  \小型门禁  \u_小型门禁_1  (
    .CLR(CPD_out), .g1(\小型门禁_1_g1 ), .g2(\小型门禁_1_g2 ), .f1(\小型门禁_1_f1 ), .f2(\小型门禁_1_f2 ), .e1(\小型门禁_1_e1 ),
    .e2(\小型门禁_1_e2 ), .d1(\小型门禁_1_d1 ), .d2(\小型门禁_1_d2 ), .c1(\小型门禁_1_c1 ), .c2(\小型门禁_1_c2 ),
    .b1(\小型门禁_1_b1 ), .b2(\小型门禁_1_b2 ), .a1(\小型门禁_1_a1 ), .a2(\小型门禁_1_a2 ), .CPU(CPU_out), .CPD(CLR_out),
    .out_4(\小型门禁_1_out_4 ));
  _7_Segment_Display u_7_segment_display_1 (
    .g(\小型门禁_1_a2 ), .f(\小型门禁_1_b2 ), .a(\小型门禁_1_c2 ), .b(\小型门禁_1_d2 ), .e(\小型门禁_1_e2 ), .d(\小型门禁_1_f2 ),
    .c(\小型门禁_1_g2 ));  // open: dp
  LED led_1 (.in(\小型门禁_1_out_4 ));
  _7_Segment_Display u_7_segment_display_2 (
    .g(\小型门禁_1_a1 ), .f(\小型门禁_1_b1 ), .a(\小型门禁_1_c1 ), .b(\小型门禁_1_d1 ), .e(\小型门禁_1_e1 ), .d(\小型门禁_1_f1 ),
    .c(\小型门禁_1_g1 ));  // open: dp
endmodule

module \显示电路  (
  input  X7,
  input  X6,
  input  X5,
  input  X4,
  input  X3,
  input  X2,
  input  X1,
  input  X0
);

  wire \译码器电路_1_y0 , \译码器电路_1_y1 , \译码器电路_1_y2 , \译码器电路_1_y3 , \译码器电路_1_y4 , \译码器电路_1_y5 , \译码器电路_1_y6 ,
       \译码器电路_2_y0 , \译码器电路_2_y1 , \译码器电路_2_y2 , \译码器电路_2_y3 , \译码器电路_2_y4 , \译码器电路_2_y5 , \译码器电路_2_y6 ;

  \译码器电路  \u_译码器电路_1  (
    .x3(X7), .x2(X6), .x1(X5), .x0(X4), .y3(\译码器电路_1_y3 ), .y2(\译码器电路_1_y2 ), .y1(\译码器电路_1_y1 ),
    .y0(\译码器电路_1_y0 ), .y6(\译码器电路_1_y6 ), .y5(\译码器电路_1_y5 ), .y4(\译码器电路_1_y4 ));
  \译码器电路  \u_译码器电路_2  (
    .x3(X3), .x2(X2), .x1(X1), .x0(X0), .y3(\译码器电路_2_y3 ), .y2(\译码器电路_2_y2 ), .y1(\译码器电路_2_y1 ),
    .y0(\译码器电路_2_y0 ), .y6(\译码器电路_2_y6 ), .y5(\译码器电路_2_y5 ), .y4(\译码器电路_2_y4 ));
  _7_Segment_Display u_7_segment_display_1 (
    .g(\译码器电路_1_y0 ), .f(\译码器电路_1_y1 ), .a(\译码器电路_1_y2 ), .b(\译码器电路_1_y3 ), .e(\译码器电路_1_y4 ),
    .d(\译码器电路_1_y5 ), .c(\译码器电路_1_y6 ));  // open: dp
  _7_Segment_Display u_7_segment_display_2 (
    .g(\译码器电路_2_y0 ), .f(\译码器电路_2_y1 ), .a(\译码器电路_2_y2 ), .b(\译码器电路_2_y3 ), .e(\译码器电路_2_y4 ),
    .d(\译码器电路_2_y5 ), .c(\译码器电路_2_y6 ));  // open: dp
endmodule

module \先行进位四位二进制加法器  (
  input  C0,
  input  A0,
  input  B0,
  input  A1,
  input  B1,
  input  A2,
  input  B2,
  input  A3,
  input  B3,
  output S0,
  output S1,
  output S2,
  output S3,
  output C4
);

  wire and_1_out, and_2_out, and_3_out, and_4_out, and_5_out, and_6_out, and_7_out, and_8_out, and_9_out,
       and_10_out, C1_out, C2_out, G0_out, G1_out, G2_out, G3_out, or_1_out, P0_out, P1_out, P2_out, P3_out;

  xor P0 (P0_out, A0, B0);
  and G0 (G0_out, A0, B0);
  xor P1 (P1_out, A1, B1);
  and G1 (G1_out, A1, B1);
  xor P2 (P2_out, A2, B2);
  and G2 (G2_out, A2, B2);
  xor P3 (P3_out, A3, B3);
  and G3 (G3_out, A3, B3);
  and and_1 (and_1_out, C0, P0_out);
  and and_2 (and_2_out, G0_out, P1_out);
  and and_3 (and_3_out, C0, P1_out, P0_out);
  and and_4 (and_4_out, G1_out, P2_out);
  and and_5 (and_5_out, P2_out, P1_out, G0_out);
  and and_6 (and_6_out, P2_out, P1_out, P0_out, C0);
  and and_7 (and_7_out, G2_out, P3_out);
  and and_8 (and_8_out, P3_out, P2_out, G1_out);
  and and_9 (and_9_out, P3_out, P2_out, P1_out, G0_out);
  and and_10 (and_10_out, P3_out, P2_out, P1_out, P0_out, C0);
  or C1 (C1_out, and_1_out, G0_out);
  or C2 (C2_out, and_2_out, and_3_out, G1_out);
  or or_1 (or_1_out, and_4_out, and_5_out, and_6_out, G2_out);
  or or_2 (C4, and_7_out, and_8_out, and_9_out, and_10_out, G3_out);
  xor xor_1 (S0, C0, P0_out);
  xor xor_2 (S1, C1_out, P1_out);
  xor xor_3 (S2, C2_out, P2_out);
  xor xor_4 (S3, or_1_out, P3_out);
endmodule

module \串行进位四位二进制加法器  (
  input  A2,
  input  A2_2,
  input  A1,
  input  B2,
  input  A0,
  input  B2_2,
  input  B1,
  input  B0,
  input  C0,
  output S3,
  output S2,
  output S1,
  output C4,
  output S0
);

  wire \二进制全加器_1_ci_1 , \二进制全加器_2_ci_1 , \二进制全加器_3_ci_1 ;

  \二进制全加器  \u_二进制全加器_1  (.A(A0), .B(B0), .Ci(C0), .Si(S0), .Ci_1(\二进制全加器_1_ci_1 ));
  \二进制全加器  \u_二进制全加器_2  (.A(A1), .B(B1), .Ci(\二进制全加器_1_ci_1 ), .Si(S1), .Ci_1(\二进制全加器_2_ci_1 ));
  \二进制全加器  \u_二进制全加器_3  (.A(A2_2), .B(B2_2), .Ci(\二进制全加器_2_ci_1 ), .Si(S2), .Ci_1(\二进制全加器_3_ci_1 ));
  \二进制全加器  \u_二进制全加器_4  (.A(A2), .B(B2), .Ci(\二进制全加器_3_ci_1 ), .Si(S3), .Ci_1(C4));
endmodule

module \二进制全加器  (
  input  A,
  input  B,
  input  Ci,
  output Si,
  output Ci_1
);

  wire nand_1_out, nand_2_out, xor_1_out;

  xor xor_1 (xor_1_out, A, B);
  nand nand_1 (nand_1_out, xor_1_out, Ci);
  nand nand_2 (nand_2_out, B, A);
  nand nand_3 (Ci_1, nand_1_out, nand_2_out);
  xor xor_2 (Si, xor_1_out, Ci);
endmodule

module \二进制半加器  (
  input  A,
  input  B,
  output S,
  output C
);

  xor xor_1 (S, A, B);
  and and_1 (C, A, B);
endmodule

module \并行进位四位加法器测试电路  (
  input  in_1,
  input  A3,
  input  A1,
  input  B3,
  input  B1,
  input  A2,
  input  A0,
  input  B2,
  input  B0,
  output S3,
  output S2,
  output S1,
  output S0,
  output C4
);

  \先行进位四位二进制加法器  \u_先行进位四位二进制加法器_1  (
    .A0(A0), .B0(B0), .A1(A1), .B1(B1), .A2(A2), .B2(B2), .A3(A3), .B3(B3), .S0(S0), .S1(S1), .S2(S2),
    .S3(S3), .C4(C4), .C0(in_1));
endmodule
