// Logisim project 2.circ as structural Verilog: 10 circuits, main circuit 4X4乘法器
module \_4X4乘法器  (
  input  [3:0] \被乘数 ,
  input  [3:0] \乘数 ,
  output [7:0] out_3
);

  wire [7:0] adder_1_out, adder_2_out, adder_3_out, adder_4_out, multiplexer_1_out, multiplexer_2_out,
       multiplexer_3_out, \左移1位电路_8位_1_out_2 , \左移1位电路_8位_2_out_2 , \左移1位电路_8位_3_out_2 ;

  Multiplexer #(.width(8), .enable("false")) multiplexer_1 (
    .in0({8{1'b0}}), .in1(adder_1_out), .out(multiplexer_1_out), .sel(\被乘数 [0]));
  Adder adder_1 (.a({8{1'b0}}), .b({4'b0000, \乘数 }), .out(adder_1_out), .cin(1'b0));  // open: cout
  \左移1位电路_8位  \u_左移1位电路_8位_1  (.in_1({4'b0000, \乘数 }), .out_2(\左移1位电路_8位_1_out_2 ));
  Adder adder_2 (.a(multiplexer_1_out), .b(\左移1位电路_8位_1_out_2 ), .out(adder_2_out), .cin(1'b0));  // open: cout
  Multiplexer #(.width(8), .enable("false")) multiplexer_2 (
    .in0(multiplexer_1_out), .in1(adder_2_out), .out(multiplexer_2_out), .sel(\被乘数 [1]));
  \左移1位电路_8位  \u_左移1位电路_8位_2  (.in_1(\左移1位电路_8位_1_out_2 ), .out_2(\左移1位电路_8位_2_out_2 ));
  Multiplexer #(.width(8), .enable("false")) multiplexer_3 (
    .in0(multiplexer_2_out), .in1(adder_3_out), .out(multiplexer_3_out), .sel(\被乘数 [2]));
  Adder adder_3 (.a(multiplexer_2_out), .b(\左移1位电路_8位_2_out_2 ), .out(adder_3_out), .cin(1'b0));  // open: cout
  \左移1位电路_8位  \u_左移1位电路_8位_3  (.in_1(\左移1位电路_8位_2_out_2 ), .out_2(\左移1位电路_8位_3_out_2 ));
  Adder adder_4 (.a(multiplexer_3_out), .b(\左移1位电路_8位_3_out_2 ), .out(adder_4_out), .cin(1'b0));  // open: cout
  Multiplexer #(.width(8), .enable("false")) multiplexer_4 (
    .in0(multiplexer_3_out), .in1(adder_4_out), .out(out_3), .sel(\被乘数 [3]));
endmodule

module \左移1位电路_8位  (
  input  [7:0] in_1,
  output [7:0] out_2
);


  assign out_2 = {in_1[6:0], 1'b0};
endmodule

module \_32X4电路  (
  input  [3:0] \被乘数 ,
  input  [31:0] \乘数 ,
  output [31:0] out_3
);

  wire [31:0] adder_1_out, adder_2_out, adder_3_out, adder_4_out, multiplexer_1_out, multiplexer_2_out,
       multiplexer_3_out, \左移1位电路_32位_1_out_2 , \左移1位电路_32位_2_out_2 , \左移1位电路_32位_3_out_2 ;

  Adder #(.width(32)) adder_1 (.a({32{1'b0}}), .b(\乘数 ), .out(adder_1_out), .cin(1'b0));  // open: cout
  \左移1位电路_32位  \u_左移1位电路_32位_1  (.out_2(\左移1位电路_32位_1_out_2 ), .in_1(\乘数 ));
  Multiplexer #(.width(32), .enable("false")) multiplexer_1 (
    .in0({32{1'b0}}), .in1(adder_1_out), .out(multiplexer_1_out), .sel(\被乘数 [0]));
  Multiplexer #(.width(32), .enable("false")) multiplexer_2 (
    .in0(multiplexer_1_out), .in1(adder_2_out), .out(multiplexer_2_out), .sel(\被乘数 [1]));
  Adder #(.width(32)) adder_2 (
    .a(multiplexer_1_out), .b(\左移1位电路_32位_1_out_2 ), .out(adder_2_out), .cin(1'b0));  // open: cout
  \左移1位电路_32位  \u_左移1位电路_32位_2  (.out_2(\左移1位电路_32位_2_out_2 ), .in_1(\左移1位电路_32位_1_out_2 ));
  Adder #(.width(32)) adder_3 (
    .a(multiplexer_2_out), .b(\左移1位电路_32位_2_out_2 ), .out(adder_3_out), .cin(1'b0));  // open: cout
  \左移1位电路_32位  \u_左移1位电路_32位_3  (.out_2(\左移1位电路_32位_3_out_2 ), .in_1(\左移1位电路_32位_2_out_2 ));
  Multiplexer #(.width(32), .enable("false")) multiplexer_3 (
    .in0(multiplexer_2_out), .in1(adder_3_out), .out(multiplexer_3_out), .sel(\被乘数 [2]));
  Adder #(.width(32)) adder_4 (
    .a(multiplexer_3_out), .b(\左移1位电路_32位_3_out_2 ), .out(adder_4_out), .cin(1'b0));  // open: cout
  Multiplexer #(.width(32), .enable("false")) multiplexer_4 (
    .in0(multiplexer_3_out), .in1(adder_4_out), .out(out_3), .sel(\被乘数 [3]));

  // Other names for the same wires on the sheet: _4_32[3:0] = \被乘数 
endmodule

module \左移1位电路_32位  (
  input  [31:0] in_1,
  output [31:0] out_2
);


  assign out_2 = {in_1[30:0], 1'b0};
endmodule

module \_32X32乘法器  (
  input  [31:0] \被乘数 ,
  input  [31:0] \乘数 ,
  output [31:0] out_3
);

  wire [31:0] adder_1_out, adder_2_out, adder_3_out, adder_4_out, adder_5_out, adder_6_out,
       \n32x4电路_1_out_3 , \n32x4电路_2_out_3 , \n32x4电路_3_out_3 , \n32x4电路_4_out_3 , \n32x4电路_5_out_3 ,
       \n32x4电路_6_out_3 , \n32x4电路_7_out_3 , \n32x4电路_8_out_3 , \左移4位电路_32位_1_out_2 , \左移4位电路_32位_2_out_2 ,
       \左移4位电路_32位_3_out_2 , \左移4位电路_32位_4_out_2 , \左移4位电路_32位_5_out_2 , \左移4位电路_32位_6_out_2 ,
       \左移4位电路_32位_7_out_2 , \左移4位电路_32位_8_out_2 , \左移4位电路_32位_9_out_2 , \左移4位电路_32位_10_out_2 ,
       \左移4位电路_32位_11_out_2 , \左移4位电路_32位_12_out_2 , \左移4位电路_32位_13_out_2 , \左移4位电路_32位_14_out_2 ,
       \左移4位电路_32位_15_out_2 , \左移4位电路_32位_16_out_2 , \左移4位电路_32位_17_out_2 , \左移4位电路_32位_18_out_2 ,
       \左移4位电路_32位_19_out_2 , \左移4位电路_32位_20_out_2 , \左移4位电路_32位_21_out_2 , \左移4位电路_32位_22_out_2 ,
       \左移4位电路_32位_23_out_2 , \左移4位电路_32位_24_out_2 , \左移4位电路_32位_25_out_2 , \左移4位电路_32位_26_out_2 ,
       \左移4位电路_32位_27_out_2 , \左移4位电路_32位_28_out_2 ;

  \_32X4电路  \u_32x4电路_1  (.\乘数 (\乘数 ), .out_3(\n32x4电路_1_out_3 ), .\被乘数 (\被乘数 [3:0]));
  \_32X4电路  \u_32x4电路_2  (.\乘数 (\乘数 ), .out_3(\n32x4电路_2_out_3 ), .\被乘数 (\被乘数 [7:4]));
  \_32X4电路  \u_32x4电路_3  (.\乘数 (\乘数 ), .out_3(\n32x4电路_3_out_3 ), .\被乘数 (\被乘数 [11:8]));
  \_32X4电路  \u_32x4电路_4  (.\乘数 (\乘数 ), .out_3(\n32x4电路_4_out_3 ), .\被乘数 (\被乘数 [15:12]));
  \_32X4电路  \u_32x4电路_5  (.\乘数 (\乘数 ), .out_3(\n32x4电路_5_out_3 ), .\被乘数 (\被乘数 [19:16]));
  \_32X4电路  \u_32x4电路_6  (.\乘数 (\乘数 ), .out_3(\n32x4电路_6_out_3 ), .\被乘数 (\被乘数 [23:20]));
  \_32X4电路  \u_32x4电路_7  (.\乘数 (\乘数 ), .out_3(\n32x4电路_7_out_3 ), .\被乘数 (\被乘数 [27:24]));
  \_32X4电路  \u_32x4电路_8  (.\乘数 (\乘数 ), .out_3(\n32x4电路_8_out_3 ), .\被乘数 (\被乘数 [31:28]));
  \左移4位电路_32位  \u_左移4位电路_32位_1  (.in_1(\n32x4电路_2_out_3 ), .out_2(\左移4位电路_32位_1_out_2 ));
  \左移4位电路_32位  \u_左移4位电路_32位_2  (.in_1(\n32x4电路_3_out_3 ), .out_2(\左移4位电路_32位_2_out_2 ));
  \左移4位电路_32位  \u_左移4位电路_32位_3  (.in_1(\n32x4电路_4_out_3 ), .out_2(\左移4位电路_32位_3_out_2 ));
  \左移4位电路_32位  \u_左移4位电路_32位_4  (.in_1(\n32x4电路_5_out_3 ), .out_2(\左移4位电路_32位_4_out_2 ));
  \左移4位电路_32位  \u_左移4位电路_32位_5  (.in_1(\n32x4电路_6_out_3 ), .out_2(\左移4位电路_32位_5_out_2 ));
  \左移4位电路_32位  \u_左移4位电路_32位_6  (.in_1(\n32x4电路_7_out_3 ), .out_2(\左移4位电路_32位_6_out_2 ));
  \左移4位电路_32位  \u_左移4位电路_32位_7  (.in_1(\n32x4电路_8_out_3 ), .out_2(\左移4位电路_32位_7_out_2 ));
  \左移4位电路_32位  \u_左移4位电路_32位_8  (.in_1(\左移4位电路_32位_2_out_2 ), .out_2(\左移4位电路_32位_8_out_2 ));
  \左移4位电路_32位  \u_左移4位电路_32位_9  (.in_1(\左移4位电路_32位_10_out_2 ), .out_2(\左移4位电路_32位_9_out_2 ));
  \左移4位电路_32位  \u_左移4位电路_32位_10  (.in_1(\左移4位电路_32位_3_out_2 ), .out_2(\左移4位电路_32位_10_out_2 ));
  \左移4位电路_32位  \u_左移4位电路_32位_11  (.in_1(\左移4位电路_32位_4_out_2 ), .out_2(\左移4位电路_32位_11_out_2 ));
  \左移4位电路_32位  \u_左移4位电路_32位_12  (.in_1(\左移4位电路_32位_13_out_2 ), .out_2(\左移4位电路_32位_12_out_2 ));
  \左移4位电路_32位  \u_左移4位电路_32位_13  (.in_1(\左移4位电路_32位_11_out_2 ), .out_2(\左移4位电路_32位_13_out_2 ));
  \左移4位电路_32位  \u_左移4位电路_32位_14  (.in_1(\左移4位电路_32位_15_out_2 ), .out_2(\左移4位电路_32位_14_out_2 ));
  \左移4位电路_32位  \u_左移4位电路_32位_15  (.in_1(\左移4位电路_32位_5_out_2 ), .out_2(\左移4位电路_32位_15_out_2 ));
  \左移4位电路_32位  \u_左移4位电路_32位_16  (.in_1(\左移4位电路_32位_14_out_2 ), .out_2(\左移4位电路_32位_16_out_2 ));
  \左移4位电路_32位  \u_左移4位电路_32位_17  (.in_1(\左移4位电路_32位_18_out_2 ), .out_2(\左移4位电路_32位_17_out_2 ));
  \左移4位电路_32位  \u_左移4位电路_32位_18  (.in_1(\左移4位电路_32位_6_out_2 ), .out_2(\左移4位电路_32位_18_out_2 ));
  \左移4位电路_32位  \u_左移4位电路_32位_19  (.in_1(\左移4位电路_32位_17_out_2 ), .out_2(\左移4位电路_32位_19_out_2 ));
  \左移4位电路_32位  \u_左移4位电路_32位_20  (.in_1(\左移4位电路_32位_7_out_2 ), .out_2(\左移4位电路_32位_20_out_2 ));
  \左移4位电路_32位  \u_左移4位电路_32位_21  (.in_1(\左移4位电路_32位_22_out_2 ), .out_2(\左移4位电路_32位_21_out_2 ));
  \左移4位电路_32位  \u_左移4位电路_32位_22  (.in_1(\左移4位电路_32位_20_out_2 ), .out_2(\左移4位电路_32位_22_out_2 ));
  \左移4位电路_32位  \u_左移4位电路_32位_23  (.in_1(\左移4位电路_32位_16_out_2 ), .out_2(\左移4位电路_32位_23_out_2 ));
  \左移4位电路_32位  \u_左移4位电路_32位_24  (.in_1(\左移4位电路_32位_25_out_2 ), .out_2(\左移4位电路_32位_24_out_2 ));
  \左移4位电路_32位  \u_左移4位电路_32位_25  (.in_1(\左移4位电路_32位_19_out_2 ), .out_2(\左移4位电路_32位_25_out_2 ));
  \左移4位电路_32位  \u_左移4位电路_32位_26  (.in_1(\左移4位电路_32位_21_out_2 ), .out_2(\左移4位电路_32位_26_out_2 ));
  \左移4位电路_32位  \u_左移4位电路_32位_27  (.in_1(\左移4位电路_32位_26_out_2 ), .out_2(\左移4位电路_32位_27_out_2 ));
  \左移4位电路_32位  \u_左移4位电路_32位_28  (.in_1(\左移4位电路_32位_27_out_2 ), .out_2(\左移4位电路_32位_28_out_2 ));
  Adder #(.width(32)) adder_1 (.a(\n32x4电路_1_out_3 ), .b(\左移4位电路_32位_1_out_2 ), .out(adder_1_out));  // open: cin, cout
  Adder #(.width(32)) adder_2 (
    .a(\左移4位电路_32位_8_out_2 ), .b(\左移4位电路_32位_9_out_2 ), .out(adder_2_out));  // open: cin, cout
  Adder #(.width(32)) adder_3 (
    .a(\左移4位电路_32位_12_out_2 ), .b(\左移4位电路_32位_23_out_2 ), .out(adder_3_out));  // open: cin, cout
  Adder #(.width(32)) adder_4 (
    .a(\左移4位电路_32位_24_out_2 ), .b(\左移4位电路_32位_28_out_2 ), .out(adder_4_out));  // open: cin, cout
  Adder #(.width(32)) adder_5 (.a(adder_1_out), .b(adder_2_out), .out(adder_5_out));  // open: cin, cout
  Adder #(.width(32)) adder_6 (.a(adder_3_out), .b(adder_4_out), .out(adder_6_out));  // open: cin, cout
  Adder #(.width(32)) adder_7 (.a(adder_5_out), .b(adder_6_out), .out(out_3));  // open: cin, cout
endmodule

module \左移4位电路_32位  (
  input  [31:0] in_1,
  output [31:0] out_2
);

  wire [31:0] \左移1位电路_32位_1_out_2 , \左移1位电路_32位_3_out_2 , \左移1位电路_32位_4_out_2 ;

  \左移1位电路_32位  \u_左移1位电路_32位_1  (.out_2(\左移1位电路_32位_1_out_2 ), .in_1(in_1));
  \左移1位电路_32位  \u_左移1位电路_32位_2  (.out_2(out_2), .in_1(\左移1位电路_32位_3_out_2 ));
  \左移1位电路_32位  \u_左移1位电路_32位_3  (.out_2(\左移1位电路_32位_3_out_2 ), .in_1(\左移1位电路_32位_4_out_2 ));
  \左移1位电路_32位  \u_左移1位电路_32位_4  (.out_2(\左移1位电路_32位_4_out_2 ), .in_1(\左移1位电路_32位_1_out_2 ));
endmodule

module \_4X4除法器  (
  input  [3:0] \被除数 ,
  input  [3:0] \除数 ,
  output [3:0] \商 ,
  output [3:0] \余数 
);

  wire comparator_1_lt, comparator_2_lt, comparator_3_lt, comparator_4_lt;
  wire [3:0] multiplexer_1_out, subtractor_1_out, subtractor_2_out, subtractor_3_out, subtractor_4_out,
       \左移1位电路_8位_1_out_2 ;
  wire [7:0] multiplexer_2_out, multiplexer_3_out, \左移1位电路_8位_4_out_2 ;
  wire [7:4] \左移1位电路_8位_1_out_2_2 , \左移1位电路_8位_2_out_2 , \左移1位电路_8位_3_out_2 ;

  \左移1位电路_8位  \u_左移1位电路_8位_1  (.in_1({4'b0000, \被除数 }), .out_2({\左移1位电路_8位_1_out_2_2 , \左移1位电路_8位_1_out_2 }));
  \左移1位电路_8位  \u_左移1位电路_8位_2  (
    .in_1({multiplexer_1_out, \左移1位电路_8位_1_out_2 }), .out_2({\左移1位电路_8位_2_out_2 , multiplexer_2_out[3:0]}));
  \左移1位电路_8位  \u_左移1位电路_8位_3  (.in_1(multiplexer_2_out), .out_2({\左移1位电路_8位_3_out_2 , multiplexer_3_out[3:0]}));
  \左移1位电路_8位  \u_左移1位电路_8位_4  (.in_1(multiplexer_3_out), .out_2(\左移1位电路_8位_4_out_2 ));
  Comparator #(.width(4), .mode("unsigned")) comparator_1 (
    .a(\左移1位电路_8位_1_out_2_2 ), .b(\除数 ), .lt(comparator_1_lt));  // open: gt, eq
  Subtractor #(.width(4)) subtractor_1 (
    .a(\左移1位电路_8位_1_out_2_2 ), .b(\除数 ), .out(subtractor_1_out));  // open: bin, bout
  Comparator #(.width(4), .mode("unsigned")) comparator_2 (
    .a(\左移1位电路_8位_2_out_2 ), .b(\除数 ), .lt(comparator_2_lt));  // open: gt, eq
  Subtractor #(.width(4)) subtractor_2 (.a(\左移1位电路_8位_2_out_2 ), .b(\除数 ), .out(subtractor_2_out));  // open: bin, bout
  Comparator #(.width(4), .mode("unsigned")) comparator_3 (
    .a(\左移1位电路_8位_3_out_2 ), .b(\除数 ), .lt(comparator_3_lt));  // open: gt, eq
  Subtractor #(.width(4)) subtractor_3 (.a(\左移1位电路_8位_3_out_2 ), .b(\除数 ), .out(subtractor_3_out));  // open: bin, bout
  Comparator #(.width(4), .mode("unsigned")) comparator_4 (
    .a(\左移1位电路_8位_4_out_2 [7:4]), .b(\除数 ), .lt(comparator_4_lt));  // open: gt, eq
  Subtractor #(.width(4)) subtractor_4 (
    .a(\左移1位电路_8位_4_out_2 [7:4]), .b(\除数 ), .out(subtractor_4_out));  // open: bin, bout
  not not_1 (\商 [3], comparator_1_lt);
  Multiplexer #(.width(4), .enable("false")) multiplexer_1 (
    .in0(subtractor_1_out), .in1(\左移1位电路_8位_1_out_2_2 ), .out(multiplexer_1_out), .sel(comparator_1_lt));
  not not_2 (\商 [2], comparator_2_lt);
  Multiplexer #(.width(4), .enable("false")) multiplexer_2 (
    .in0(subtractor_2_out), .in1(\左移1位电路_8位_2_out_2 ), .out(multiplexer_2_out[7:4]), .sel(comparator_2_lt));
  not not_3 (\商 [1], comparator_3_lt);
  Multiplexer #(.width(4), .enable("false")) multiplexer_3 (
    .in0(subtractor_3_out), .in1(\左移1位电路_8位_3_out_2 ), .out(multiplexer_3_out[7:4]), .sel(comparator_3_lt));
  not not_4 (\商 [0], comparator_4_lt);
  Multiplexer #(.width(4), .enable("false")) multiplexer_4 (
    .in0(subtractor_4_out), .in1(\左移1位电路_8位_4_out_2 [7:4]), .out(\余数 ), .sel(comparator_4_lt));
endmodule

module \_32X32除法器电路单元  (
  input  [31:0] in_1,
  input  [31:0] in_2,
  input  [31:0] in_3,
  output [31:0] out_4,
  output [31:0] out_5,
  output out_6
);

  wire comparator_1_lt;
  wire [31:0] subtractor_1_out;

  Subtractor #(.width(32)) subtractor_1 (
    .a({in_3[30:0], in_1[31]}), .b(in_2), .out(subtractor_1_out));  // open: bin, bout
  Multiplexer #(.width(32), .enable("false")) multiplexer_1 (
    .in0(subtractor_1_out), .in1({in_3[30:0], in_1[31]}), .out(out_5), .sel(comparator_1_lt));
  Comparator #(.width(32), .mode("unsigned")) comparator_1 (
    .a({in_3[30:0], in_1[31]}), .b(in_2), .lt(comparator_1_lt));  // open: gt, eq
  not not_1 (out_6, comparator_1_lt);

  assign out_4 = {in_1[30:0], 1'b0};
endmodule

module \_32X32除法器  (
  input  [31:0] \被除数 ,
  input  [31:0] \除数 ,
  output [31:0] \余数 ,
  output [31:0] \商 
);

  wire [31:0] \n32x32除法器电路单元_1_out_4 , \n32x32除法器电路单元_1_out_5 , \n32x32除法器电路单元_2_out_4 ,
       \n32x32除法器电路单元_2_out_5 , \n32x32除法器电路单元_3_out_4 , \n32x32除法器电路单元_3_out_5 , \n32x32除法器电路单元_4_out_4 ,
       \n32x32除法器电路单元_4_out_5 , \n32x32除法器电路单元_5_out_4 , \n32x32除法器电路单元_5_out_5 , \n32x32除法器电路单元_6_out_4 ,
       \n32x32除法器电路单元_6_out_5 , \n32x32除法器电路单元_7_out_4 , \n32x32除法器电路单元_7_out_5 , \n32x32除法器电路单元_8_out_4 ,
       \n32x32除法器电路单元_8_out_5 , \n32x32除法器电路单元_9_out_4 , \n32x32除法器电路单元_9_out_5 , \n32x32除法器电路单元_10_out_4 ,
       \n32x32除法器电路单元_10_out_5 , \n32x32除法器电路单元_11_out_4 , \n32x32除法器电路单元_11_out_5 ,
       \n32x32除法器电路单元_12_out_4 , \n32x32除法器电路单元_12_out_5 , \n32x32除法器电路单元_13_out_4 ,
       \n32x32除法器电路单元_13_out_5 , \n32x32除法器电路单元_14_out_4 , \n32x32除法器电路单元_14_out_5 ,
       \n32x32除法器电路单元_15_out_4 , \n32x32除法器电路单元_15_out_5 , \n32x32除法器电路单元_16_out_4 ,
       \n32x32除法器电路单元_16_out_5 , \n32x32除法器电路单元_17_out_4 , \n32x32除法器电路单元_17_out_5 ,
       \n32x32除法器电路单元_18_out_4 , \n32x32除法器电路单元_18_out_5 , \n32x32除法器电路单元_19_out_4 ,
       \n32x32除法器电路单元_19_out_5 , \n32x32除法器电路单元_20_out_4 , \n32x32除法器电路单元_20_out_5 ,
       \n32x32除法器电路单元_21_out_4 , \n32x32除法器电路单元_21_out_5 , \n32x32除法器电路单元_22_out_4 ,
       \n32x32除法器电路单元_22_out_5 , \n32x32除法器电路单元_23_out_4 , \n32x32除法器电路单元_23_out_5 ,
       \n32x32除法器电路单元_24_out_4 , \n32x32除法器电路单元_24_out_5 , \n32x32除法器电路单元_25_out_4 ,
       \n32x32除法器电路单元_25_out_5 , \n32x32除法器电路单元_26_out_4 , \n32x32除法器电路单元_26_out_5 ,
       \n32x32除法器电路单元_27_out_4 , \n32x32除法器电路单元_27_out_5 , \n32x32除法器电路单元_28_out_4 ,
       \n32x32除法器电路单元_28_out_5 , \n32x32除法器电路单元_29_out_4 , \n32x32除法器电路单元_29_out_5 ,
       \n32x32除法器电路单元_30_out_4 , \n32x32除法器电路单元_30_out_5 , \n32x32除法器电路单元_31_out_4 , \n32x32除法器电路单元_31_out_5 ;

  \_32X32除法器电路单元  \u_32x32除法器电路单元_1  (
    .in_1(\被除数 ), .in_2(\除数 ), .in_3({32{1'b0}}), .out_5(\n32x32除法器电路单元_1_out_5 ), .out_6(\商 [31]),
    .out_4(\n32x32除法器电路单元_1_out_4 ));
  \_32X32除法器电路单元  \u_32x32除法器电路单元_2  (
    .in_1(\n32x32除法器电路单元_1_out_4 ), .in_2(\除数 ), .in_3(\n32x32除法器电路单元_1_out_5 ),
    .out_5(\n32x32除法器电路单元_2_out_5 ), .out_6(\商 [30]), .out_4(\n32x32除法器电路单元_2_out_4 ));
  \_32X32除法器电路单元  \u_32x32除法器电路单元_3  (
    .in_1(\n32x32除法器电路单元_2_out_4 ), .in_2(\除数 ), .in_3(\n32x32除法器电路单元_2_out_5 ),
    .out_5(\n32x32除法器电路单元_3_out_5 ), .out_6(\商 [29]), .out_4(\n32x32除法器电路单元_3_out_4 ));
  \_32X32除法器电路单元  \u_32x32除法器电路单元_4  (
    .in_1(\n32x32除法器电路单元_3_out_4 ), .in_2(\除数 ), .in_3(\n32x32除法器电路单元_3_out_5 ),
    .out_5(\n32x32除法器电路单元_4_out_5 ), .out_6(\商 [28]), .out_4(\n32x32除法器电路单元_4_out_4 ));
  \_32X32除法器电路单元  \u_32x32除法器电路单元_5  (
    .in_1(\n32x32除法器电路单元_4_out_4 ), .in_2(\除数 ), .in_3(\n32x32除法器电路单元_4_out_5 ),
    .out_5(\n32x32除法器电路单元_5_out_5 ), .out_6(\商 [27]), .out_4(\n32x32除法器电路单元_5_out_4 ));
  \_32X32除法器电路单元  \u_32x32除法器电路单元_6  (
    .in_1(\n32x32除法器电路单元_5_out_4 ), .in_2(\除数 ), .in_3(\n32x32除法器电路单元_5_out_5 ),
    .out_5(\n32x32除法器电路单元_6_out_5 ), .out_6(\商 [26]), .out_4(\n32x32除法器电路单元_6_out_4 ));
  \_32X32除法器电路单元  \u_32x32除法器电路单元_7  (
    .in_1(\n32x32除法器电路单元_6_out_4 ), .in_2(\除数 ), .in_3(\n32x32除法器电路单元_6_out_5 ),
    .out_5(\n32x32除法器电路单元_7_out_5 ), .out_6(\商 [25]), .out_4(\n32x32除法器电路单元_7_out_4 ));
  \_32X32除法器电路单元  \u_32x32除法器电路单元_8  (
    .in_1(\n32x32除法器电路单元_7_out_4 ), .in_2(\除数 ), .in_3(\n32x32除法器电路单元_7_out_5 ),
    .out_5(\n32x32除法器电路单元_8_out_5 ), .out_6(\商 [24]), .out_4(\n32x32除法器电路单元_8_out_4 ));
  \_32X32除法器电路单元  \u_32x32除法器电路单元_9  (
    .in_1(\n32x32除法器电路单元_8_out_4 ), .in_2(\除数 ), .in_3(\n32x32除法器电路单元_8_out_5 ),
    .out_5(\n32x32除法器电路单元_9_out_5 ), .out_6(\商 [23]), .out_4(\n32x32除法器电路单元_9_out_4 ));
  \_32X32除法器电路单元  \u_32x32除法器电路单元_10  (
    .in_1(\n32x32除法器电路单元_9_out_4 ), .in_2(\除数 ), .in_3(\n32x32除法器电路单元_9_out_5 ),
    .out_5(\n32x32除法器电路单元_10_out_5 ), .out_6(\商 [22]), .out_4(\n32x32除法器电路单元_10_out_4 ));
  \_32X32除法器电路单元  \u_32x32除法器电路单元_11  (
    .in_1(\n32x32除法器电路单元_10_out_4 ), .in_2(\除数 ), .in_3(\n32x32除法器电路单元_10_out_5 ),
    .out_5(\n32x32除法器电路单元_11_out_5 ), .out_6(\商 [21]), .out_4(\n32x32除法器电路单元_11_out_4 ));
  \_32X32除法器电路单元  \u_32x32除法器电路单元_12  (
    .in_1(\n32x32除法器电路单元_11_out_4 ), .in_2(\除数 ), .in_3(\n32x32除法器电路单元_11_out_5 ),
    .out_5(\n32x32除法器电路单元_12_out_5 ), .out_6(\商 [20]), .out_4(\n32x32除法器电路单元_12_out_4 ));
  \_32X32除法器电路单元  \u_32x32除法器电路单元_13  (
    .in_1(\n32x32除法器电路单元_12_out_4 ), .in_2(\除数 ), .in_3(\n32x32除法器电路单元_12_out_5 ),
    .out_5(\n32x32除法器电路单元_13_out_5 ), .out_6(\商 [19]), .out_4(\n32x32除法器电路单元_13_out_4 ));
  \_32X32除法器电路单元  \u_32x32除法器电路单元_14  (
    .in_1(\n32x32除法器电路单元_13_out_4 ), .in_2(\除数 ), .in_3(\n32x32除法器电路单元_13_out_5 ),
    .out_5(\n32x32除法器电路单元_14_out_5 ), .out_6(\商 [18]), .out_4(\n32x32除法器电路单元_14_out_4 ));
  \_32X32除法器电路单元  \u_32x32除法器电路单元_15  (
    .in_1(\n32x32除法器电路单元_14_out_4 ), .in_2(\除数 ), .in_3(\n32x32除法器电路单元_14_out_5 ),
    .out_5(\n32x32除法器电路单元_15_out_5 ), .out_6(\商 [17]), .out_4(\n32x32除法器电路单元_15_out_4 ));
  \_32X32除法器电路单元  \u_32x32除法器电路单元_16  (
    .in_1(\n32x32除法器电路单元_15_out_4 ), .in_2(\除数 ), .in_3(\n32x32除法器电路单元_15_out_5 ),
    .out_5(\n32x32除法器电路单元_16_out_5 ), .out_6(\商 [16]), .out_4(\n32x32除法器电路单元_16_out_4 ));
  \_32X32除法器电路单元  \u_32x32除法器电路单元_17  (
    .in_1(\n32x32除法器电路单元_16_out_4 ), .in_2(\除数 ), .in_3(\n32x32除法器电路单元_16_out_5 ),
    .out_5(\n32x32除法器电路单元_17_out_5 ), .out_6(\商 [15]), .out_4(\n32x32除法器电路单元_17_out_4 ));
  \_32X32除法器电路单元  \u_32x32除法器电路单元_18  (
    .in_1(\n32x32除法器电路单元_17_out_4 ), .in_2(\除数 ), .in_3(\n32x32除法器电路单元_17_out_5 ),
    .out_5(\n32x32除法器电路单元_18_out_5 ), .out_6(\商 [14]), .out_4(\n32x32除法器电路单元_18_out_4 ));
  \_32X32除法器电路单元  \u_32x32除法器电路单元_19  (
    .in_1(\n32x32除法器电路单元_18_out_4 ), .in_2(\除数 ), .in_3(\n32x32除法器电路单元_18_out_5 ),
    .out_5(\n32x32除法器电路单元_19_out_5 ), .out_6(\商 [13]), .out_4(\n32x32除法器电路单元_19_out_4 ));
  \_32X32除法器电路单元  \u_32x32除法器电路单元_20  (
    .in_1(\n32x32除法器电路单元_19_out_4 ), .in_2(\除数 ), .in_3(\n32x32除法器电路单元_19_out_5 ),
    .out_5(\n32x32除法器电路单元_20_out_5 ), .out_6(\商 [12]), .out_4(\n32x32除法器电路单元_20_out_4 ));
  \_32X32除法器电路单元  \u_32x32除法器电路单元_21  (
    .in_1(\n32x32除法器电路单元_20_out_4 ), .in_2(\除数 ), .in_3(\n32x32除法器电路单元_20_out_5 ),
    .out_5(\n32x32除法器电路单元_21_out_5 ), .out_6(\商 [11]), .out_4(\n32x32除法器电路单元_21_out_4 ));
  \_32X32除法器电路单元  \u_32x32除法器电路单元_22  (
    .in_1(\n32x32除法器电路单元_21_out_4 ), .in_2(\除数 ), .in_3(\n32x32除法器电路单元_21_out_5 ),
    .out_5(\n32x32除法器电路单元_22_out_5 ), .out_6(\商 [10]), .out_4(\n32x32除法器电路单元_22_out_4 ));
  \_32X32除法器电路单元  \u_32x32除法器电路单元_23  (
    .in_1(\n32x32除法器电路单元_22_out_4 ), .in_2(\除数 ), .in_3(\n32x32除法器电路单元_22_out_5 ),
    .out_5(\n32x32除法器电路单元_23_out_5 ), .out_6(\商 [9]), .out_4(\n32x32除法器电路单元_23_out_4 ));
  \_32X32除法器电路单元  \u_32x32除法器电路单元_24  (
    .in_1(\n32x32除法器电路单元_23_out_4 ), .in_2(\除数 ), .in_3(\n32x32除法器电路单元_23_out_5 ),
    .out_5(\n32x32除法器电路单元_24_out_5 ), .out_6(\商 [8]), .out_4(\n32x32除法器电路单元_24_out_4 ));
  \_32X32除法器电路单元  \u_32x32除法器电路单元_25  (
    .in_1(\n32x32除法器电路单元_24_out_4 ), .in_2(\除数 ), .in_3(\n32x32除法器电路单元_24_out_5 ),
    .out_5(\n32x32除法器电路单元_25_out_5 ), .out_6(\商 [7]), .out_4(\n32x32除法器电路单元_25_out_4 ));
  \_32X32除法器电路单元  \u_32x32除法器电路单元_26  (
    .in_1(\n32x32除法器电路单元_25_out_4 ), .in_2(\除数 ), .in_3(\n32x32除法器电路单元_25_out_5 ),
    .out_5(\n32x32除法器电路单元_26_out_5 ), .out_6(\商 [6]), .out_4(\n32x32除法器电路单元_26_out_4 ));
  \_32X32除法器电路单元  \u_32x32除法器电路单元_27  (
    .in_1(\n32x32除法器电路单元_26_out_4 ), .in_2(\除数 ), .in_3(\n32x32除法器电路单元_26_out_5 ),
    .out_5(\n32x32除法器电路单元_27_out_5 ), .out_6(\商 [5]), .out_4(\n32x32除法器电路单元_27_out_4 ));
  \_32X32除法器电路单元  \u_32x32除法器电路单元_28  (
    .in_1(\n32x32除法器电路单元_27_out_4 ), .in_2(\除数 ), .in_3(\n32x32除法器电路单元_27_out_5 ),
    .out_5(\n32x32除法器电路单元_28_out_5 ), .out_6(\商 [4]), .out_4(\n32x32除法器电路单元_28_out_4 ));
  \_32X32除法器电路单元  \u_32x32除法器电路单元_29  (
    .in_1(\n32x32除法器电路单元_28_out_4 ), .in_2(\除数 ), .in_3(\n32x32除法器电路单元_28_out_5 ),
    .out_5(\n32x32除法器电路单元_29_out_5 ), .out_6(\商 [3]), .out_4(\n32x32除法器电路单元_29_out_4 ));
  \_32X32除法器电路单元  \u_32x32除法器电路单元_30  (
    .in_1(\n32x32除法器电路单元_29_out_4 ), .in_2(\除数 ), .in_3(\n32x32除法器电路单元_29_out_5 ),
    .out_5(\n32x32除法器电路单元_30_out_5 ), .out_6(\商 [2]), .out_4(\n32x32除法器电路单元_30_out_4 ));
  \_32X32除法器电路单元  \u_32x32除法器电路单元_31  (
    .in_1(\n32x32除法器电路单元_30_out_4 ), .in_2(\除数 ), .in_3(\n32x32除法器电路单元_30_out_5 ),
    .out_5(\n32x32除法器电路单元_31_out_5 ), .out_6(\商 [1]), .out_4(\n32x32除法器电路单元_31_out_4 ));
  \_32X32除法器电路单元  \u_32x32除法器电路单元_32  (
    .in_1(\n32x32除法器电路单元_31_out_4 ), .in_2(\除数 ), .in_3(\n32x32除法器电路单元_31_out_5 ), .out_5(\余数 ),
    .out_6(\商 [0]));  // open: out_4
endmodule

module \测试  (
  input  [3:0] in_1,
  input  [3:0] in_2,
  input  [3:0] in_3,
  input  [31:0] in_4,
  input  [31:0] in_5,
  input  [3:0] in_6,
  input  [31:0] in_7,
  input  [3:0] in_8,
  input  [31:0] in_9,
  input  [31:0] in_10,
  output [7:0] out_11,
  output [31:0] out_12,
  output [31:0] out_13,
  output [3:0] out_14,
  output [3:0] out_15,
  output [31:0] out_16,
  output [31:0] out_17
);

  // Probe on in_1
  // Probe on in_2
  // Probe on in_8
  // Probe on in_6
  // Probe on in_9
  \_4X4乘法器  \u_4x4乘法器_1  (.\被乘数 (in_1), .out_3(out_11), .\乘数 (in_2));
  // Probe on in_4
  // Probe on in_3
  \_4X4除法器  \u_4x4除法器_1  (.\被除数 (in_6), .\除数 (in_8), .\商 (out_14), .\余数 (out_15));
  // Probe on in_10
  // Probe on out_11
  \_32X4电路  \u_32x4电路_1  (.\乘数 (in_4), .out_3(out_12), .\被乘数 (in_3));
  // Probe on out_14
  \_32X32除法器  \u_32x32除法器_1  (.\被除数 (in_9), .\除数 (in_10), .\商 (out_16), .\余数 (out_17));
  // Probe on out_12
  // Probe on out_15
  // Probe on out_16
  // Probe on in_5
  // Probe on out_17
  // Probe on in_7
  \_32X32乘法器  \u_32x32乘法器_1  (.\被乘数 (in_5), .\乘数 (in_7), .out_3(out_13));
  // Probe on out_13
endmodule
