// Logisim project 3.circ as structural Verilog: 13 circuits, main circuit mod10计数器
module \mod10计数器  (
  input  CPU,
  input  CPD,
  input  CLR,
  output Y1,
  output Y2,
  output CF,
  output Y3,
  output Y4
);

  wire and_1_out, and_2_out, and_3_out, and_4_out, and_5_out, and_6_out, and_7_out, and_8_out, and_9_out,
       and_10_out, and_12_out, and_13_out, and_14_out, and_15_out, and_16_out, and_17_out, CP, D1, D2, D3,
       D4, not_1_out, x, x_minus, y2_t, y3_t, y4_t;

  D_Flip_Flop #(.trigger("falling")) d_ff_1 (.clk(CP), .D(D1), .Q(Y1), .Qn(D1), .reset(CLR));  // open: preset, en
  D_Flip_Flop #(.trigger("falling")) d_ff_2 (.clk(CP), .D(D2), .Q(Y2), .Qn(y2_t), .reset(CLR));  // open: preset, en
  D_Flip_Flop #(.trigger("falling")) d_ff_3 (.clk(CP), .D(D3), .Q(Y3), .Qn(y3_t), .reset(CLR));  // open: preset, en
  D_Flip_Flop #(.trigger("falling")) d_ff_4 (.clk(CP), .D(D4), .Q(Y4), .Qn(y4_t), .reset(CLR));  // open: preset, en
  and and_1 (and_1_out, x_minus, Y2, Y1);
  and and_2 (and_2_out, x_minus, Y3, D1, y2_t);
  and and_3 (and_3_out, x_minus, Y4, D1);
  and and_4 (and_4_out, x, y2_t, Y1, y4_t);
  and and_5 (and_5_out, x, Y2, D1);
  or or_1 (D2, and_1_out, and_2_out, and_5_out, and_3_out, and_4_out);
  not not_1 (not_1_out, CPD);
  and and_6 (and_6_out, x, Y1, Y2, y3_t);
  and and_7 (and_7_out, x_minus, Y3, Y1);
  and and_8 (and_8_out, Y2, Y3, D1);
  and and_9 (and_9_out, x_minus, Y4, D1);
  and and_10 (and_10_out, x, Y3, y2_t);
  or or_2 (CP, CPU, CPD);
  and and_11 (x, CPU, not_1_out);
  not not_2 (x_minus, x);
  or or_3 (D3, and_6_out, and_7_out, and_8_out, and_9_out, and_10_out);
  and and_12 (and_12_out, x_minus, D1, y2_t, y3_t, y4_t);
  and and_13 (and_13_out, x_minus, Y4, Y1);
  and and_14 (and_14_out, x, Y1, Y2, Y3);
  and and_15 (and_15_out, x, Y4, D1);
  or or_4 (D4, and_12_out, and_13_out, and_14_out, and_15_out);
  and and_16 (and_16_out, CPU, ~Y2, Y1, ~Y3, Y4);  // AND_Gate
  and and_17 (and_17_out, CPD, ~Y2, ~Y1, ~Y3, ~Y4);  // AND_Gate
  or or_5 (CF, and_16_out, and_17_out);

  // Other names for the same wires on the sheet: x1 = Y1; x2 = Y2; x3 = Y3; x4 = Y4; y1_t = D1
endmodule

module \mod6计数器  (
  input  CPU,
  input  CPD,
  input  CLR,
  output Y1,
  output Y2,
  output Y3,
  output CF
);

  wire and_2_out, and_3_out, and_4_out, and_5_out, and_6_out, and_7_out, and_8_out, and_9_out, CP, D1, D2,
       D3, not_1_out, x, x_minus, y2_t, y3_t;

  not not_1 (not_1_out, CPD);
  or or_1 (CP, CPU, CPD);
  and and_1 (x, CPU, not_1_out);
  and and_2 (and_2_out, x_minus, Y2, Y1);
  and and_3 (and_3_out, x_minus, Y3, D1);
  and and_4 (and_4_out, x, y3_t, y2_t, Y1);
  and and_5 (and_5_out, x, Y2, D1);
  not not_2 (x_minus, x);
  or or_2 (D2, and_2_out, and_3_out, and_4_out, and_5_out);
  and and_6 (and_6_out, x_minus, Y3, Y1);
  and and_7 (and_7_out, x, Y2, Y1);
  and and_8 (and_8_out, x_minus, y3_t, y2_t, D1);
  and and_9 (and_9_out, x, Y3, D1);
  or or_3 (D3, and_6_out, and_7_out, and_8_out, and_9_out);
  D_Flip_Flop #(.trigger("falling")) d_ff_1 (.clk(CP), .D(D1), .Q(Y1), .Qn(D1), .reset(CLR));  // open: preset, en
  D_Flip_Flop #(.trigger("falling")) d_ff_2 (.clk(CP), .D(D2), .Q(Y2), .Qn(y2_t), .reset(CLR));  // open: preset, en
  D_Flip_Flop #(.trigger("falling")) d_ff_3 (.clk(CP), .D(D3), .Q(Y3), .Qn(y3_t), .reset(CLR));  // open: preset, en
  and and_10 (CF, CPU, Y1, ~Y2, Y3);  // AND_Gate

  // Other names for the same wires on the sheet: x1 = Y1; x2 = Y2; x3 = Y3; y1_t = D1
endmodule

module \mod60计数器  (
  input  CLR,
  input  ADJ,
  input  CPU,
  input  CPD,
  output Q1D,
  output Q1C,
  output Q1B,
  output Q1A,
  output Q2D,
  output Q2C,
  output Q2B,
  output Q2A,
  output out_13
);

  wire and_1_out, and_2_out, and_3_out, \mod10计数器_1_cf ;

  and and_1 (and_1_out, ADJ, CPD);
  and and_2 (and_2_out, Q1D, \mod10计数器_1_cf );
  \mod10计数器  \mod10计数器_1  (
    .CPU(CPU), .CPD(and_1_out), .Y1(Q1A), .Y2(Q1B), .Y3(Q1C), .Y4(Q1D), .CLR(CLR), .CF(\mod10计数器_1_cf ));
  and and_3 (and_3_out, ~Q1D, \mod10计数器_1_cf );  // AND_Gate
  \mod6计数器  \mod6计数器_1  (.CPU(and_2_out), .CPD(and_3_out), .Y1(Q2A), .Y2(Q2B), .Y3(Q2C), .CF(out_13), .CLR(CLR));

  assign Q2D = 1'b0;
endmodule

module mod3 (
  input  CPU,
  input  CPD,
  input  in_3,
  output out_4,
  output out_5,
  output out_6
);

  wire and_3_out, and_4_out, and_5_out, and_6_out, CP, d_ff_1_qn, d_ff_2_qn, not_1_out, or_2_out, or_3_out,
       x, x_minus;

  not not_1 (not_1_out, CPD);
  D_Flip_Flop #(.trigger("falling")) d_ff_1 (
    .clk(CP), .D(or_2_out), .Q(out_5), .Qn(d_ff_1_qn), .reset(in_3));  // open: preset, en
  D_Flip_Flop #(.trigger("falling")) d_ff_2 (
    .clk(CP), .D(or_3_out), .Q(out_4), .Qn(d_ff_2_qn), .reset(in_3));  // open: preset, en
  and and_1 (out_6, x, out_4);
  or or_1 (CP, CPU, CPD);
  and and_2 (x, CPU, not_1_out);
  not not_2 (x_minus, x);
  and and_3 (and_3_out, x, d_ff_1_qn, d_ff_2_qn);
  and and_4 (and_4_out, x_minus, out_4);
  or or_2 (or_2_out, and_3_out, and_4_out);
  and and_5 (and_5_out, x, out_5);
  and and_6 (and_6_out, x_minus, d_ff_2_qn, d_ff_1_qn);
  or or_3 (or_3_out, and_5_out, and_6_out);
endmodule

module \mod12_24计数器  (
  input  SET,
  input  ADJ,
  input  CPU,
  input  CLR,
  input  CPD,
  output QCC,
  output out_7,
  output out_8,
  output out_9,
  output out_10,
  output out_11,
  output out_12,
  output out_13,
  output out_14
);

  wire and_1_out, and_2_out, and_3_out, and_4_out, and_5_out, and_6_out, and_7_out, and_8_out, and_9_out,
       and_10_out, and_11_out, \mod10计数器_1_cf , \mod10计数器_2_cf , not_1_out, not_2_out, or_1_out, or_2_out,
       or_3_out, or_4_out, temp_1_out_2;
  wire [1:0] mod3_1_out_5, mod3_2_out_5;
  wire [3:0] \mod10计数器_1_y1 , \mod10计数器_2_y1 ;

  Button button_1 ();  // open: out
  buf and_1 (and_1_out, CPU);  // AND_Gate
  and and_2 (and_2_out, ADJ, CPD);
  or or_1 (or_1_out, or_3_out, and_3_out);
  temp temp_1 (.in_1(\mod10计数器_1_y1 [3]), .out_2(temp_1_out_2));
  or or_2 (or_2_out, or_4_out, and_4_out);
  and and_3 (and_3_out, temp_1_out_2, ~\mod10计数器_1_y1 [2], ~\mod10计数器_1_y1 [1], \mod10计数器_1_y1 [0], mod3_1_out_5[1], ~mod3_1_out_5[0]);  // AND_Gate
  \mod10计数器  \mod10计数器_1  (
    .CPU(and_1_out), .CPD(and_2_out), .Y1(\mod10计数器_1_y1 [0]), .Y2(\mod10计数器_1_y1 [1]),
    .Y3(\mod10计数器_1_y1 [2]), .Y4(\mod10计数器_1_y1 [3]), .CLR(or_1_out), .CF(\mod10计数器_1_cf ));
  and and_4 (and_4_out, \mod10计数器_2_y1 [3], ~\mod10计数器_2_y1 [2], ~\mod10计数器_2_y1 [1], \mod10计数器_2_y1 [0], mod3_2_out_5[1], ~mod3_2_out_5[0]);  // AND_Gate
  \mod10计数器  \mod10计数器_2  (
    .CPU(and_1_out), .CPD(and_2_out), .Y1(\mod10计数器_2_y1 [0]), .Y2(\mod10计数器_2_y1 [1]),
    .Y3(\mod10计数器_2_y1 [2]), .Y4(\mod10计数器_2_y1 [3]), .CLR(or_2_out), .CF(\mod10计数器_2_cf ));
  and and_5 (and_5_out, \mod10计数器_1_y1 [3], \mod10计数器_1_cf );
  and and_6 (and_6_out, ~\mod10计数器_1_y1 [3], \mod10计数器_1_cf );  // AND_Gate
  and and_7 (and_7_out, \mod10计数器_2_y1 [3], \mod10计数器_2_cf );
  and and_8 (and_8_out, ~\mod10计数器_2_y1 [3], \mod10计数器_2_cf );  // AND_Gate
  and and_9 (and_9_out, \mod10计数器_1_y1 [2], mod3_1_out_5[1], ~mod3_1_out_5[0]);  // AND_Gate
  mod3 mod3_1 (
    .CPU(and_5_out), .CPD(and_6_out), .in_3(or_1_out), .out_4(mod3_1_out_5[1]), .out_5(mod3_1_out_5[0]));  // open: out_6
  and and_10 (and_10_out, \mod10计数器_2_y1 [1], ~mod3_2_out_5[1], mod3_2_out_5[0]);  // AND_Gate
  mod3 mod3_2 (
    .CPU(and_7_out), .CPD(and_8_out), .in_3(or_2_out), .out_4(mod3_2_out_5[1]), .out_5(mod3_2_out_5[0]));  // open: out_6
  or or_3 (or_3_out, and_9_out, CLR);
  not not_1 (not_1_out, SET);
  or or_4 (or_4_out, and_10_out, CLR, CLR);
  Multiplexer #(.width(4), .enable("false")) multiplexer_1 (
    .in0(\mod10计数器_1_y1 ), .in1(\mod10计数器_2_y1 ), .out({out_10, out_9, out_8, out_7}), .sel(not_1_out));
  Multiplexer #(.width(4), .enable("false")) multiplexer_2 (
    .in0({2'b00, mod3_1_out_5}), .in1({2'b00, mod3_2_out_5}), .out({out_14, out_13, out_12, out_11}),
    .sel(not_1_out));
  not not_2 (not_2_out, CLR);
  and and_11 (and_11_out, or_3_out, ~CLR);  // AND_Gate
  Multiplexer #(.enable("false")) multiplexer_3 (.in0(QCC), .in1(and_11_out), .sel(not_1_out));  // open: out
  and and_12 (QCC, or_4_out, not_2_out);
endmodule

module \LED电路  (
  input  AM_PM,
  input  TT,
  output [4:0] out_3,
  output [4:0] out_4,
  output [4:0] out_5,
  output [4:0] out_6
);

  wire not_1_out;
  wire [4:0] multiplexer_1_out, multiplexer_2_out;

  not not_1 (not_1_out, AM_PM);
  Multiplexer #(.width(5), .enable("false")) multiplexer_1 (
    .in0(5'b10000), .in1(5'b00001), .out(multiplexer_1_out), .sel(not_1_out));
  Multiplexer #(.width(5), .enable("false")) multiplexer_2 (
    .in0(5'b10100), .in1(5'b00101), .out(multiplexer_2_out), .sel(not_1_out));
  Multiplexer #(.width(5), .enable("false")) multiplexer_3 (
    .in0({5{1'b0}}), .in1(multiplexer_1_out), .out(out_3), .sel(TT));
  Multiplexer #(.width(5), .enable("false")) multiplexer_4 (
    .in0({5{1'b0}}), .in1(multiplexer_2_out), .out(out_5), .sel(TT));
  Multiplexer #(.width(5), .enable("false")) multiplexer_5 (.in0({5{1'b0}}), .in1({5{1'b1}}), .out(out_4), .sel(TT));

  assign out_6 = out_3;
endmodule

module \脉冲1HZ电路  (
  input  in_1,
  output out_2
);

  wire t_ff_1_q, t_ff_2_q;

  T_Flip_Flop t_ff_1 (.clk(in_1), .T(1'b1), .Q(t_ff_1_q));  // open: Qn, preset, reset, en
  T_Flip_Flop t_ff_2 (.clk(t_ff_1_q), .T(1'b1), .Q(t_ff_2_q));  // open: Qn, preset, reset, en
  T_Flip_Flop t_ff_3 (.clk(t_ff_2_q), .T(1'b1), .Q(out_2));  // open: Qn, preset, reset, en
endmodule

module \整点报时电路  (
  input  [3:0] in_1,
  input  [3:0] in_2,
  input  [3:0] in_3,
  input  [3:0] in_4,
  output out_5
);

  wire comparator_1_eq, comparator_2_eq, comparator_3_eq, comparator_4_eq;

  Comparator #(.width(4), .mode("unsigned")) comparator_1 (
    .a(in_1), .b(4'b0101), .eq(comparator_1_eq));  // open: gt, lt
  Comparator #(.width(4), .mode("unsigned")) comparator_2 (
    .a(in_2), .b(4'b1001), .eq(comparator_2_eq));  // open: gt, lt
  Comparator #(.width(4), .mode("unsigned")) comparator_3 (
    .a(in_3), .b(4'b0101), .eq(comparator_3_eq));  // open: gt, lt
  Comparator #(.width(1), .mode("unsigned")) comparator_4 (
    .a(in_4[0]), .b(1'b0), .eq(comparator_4_eq));  // open: gt, lt
  and and_1 (out_5, comparator_1_eq, comparator_2_eq, comparator_3_eq, comparator_4_eq);
endmodule

module \电子钟  (
  input  CP,
  input  ADJ1,
  input  ADJ0,
  input  CPU,
  input  CPD,
  input  SET,
  input  CLR,
  output [3:0] out_8,
  output [3:0] out_9,
  output [3:0] out_10,
  output \报时 ,
  output [3:0] out_12,
  output [3:0] out_13,
  output [3:0] out_14,
  output [4:0] out_15,
  output [4:0] out_16,
  output [4:0] out_17,
  output [4:0] out_18
);

  wire and_1_out, and_2_out, and_3_out, and_4_out, and_5_out, and_6_out, and_7_out, and_8_out, and_10_out,
       \mod12_24计数器_1_qcc , \mod60计数器_1_out_13 , \mod60计数器_2_out_13 , not_1_out, not_2_out, or_1_out,
       or_2_out, or_3_out, t_ff_1_q, \脉冲1hz电路_1_out_2 ;

  \脉冲1HZ电路  \u_脉冲1hz电路_1  (.in_1(CP), .out_2(\脉冲1hz电路_1_out_2 ));
  buf and_1 (and_1_out, \脉冲1hz电路_1_out_2 );  // AND_Gate
  and and_2 (and_2_out, CPU, ADJ0);
  and and_3 (and_3_out, ADJ1, CPU);
  and and_4 (and_4_out, CPD, ADJ0);
  not not_1 (not_1_out, ADJ1);
  and and_5 (and_5_out, not_1_out, and_2_out);
  and and_6 (and_6_out, and_2_out, ~not_1_out);  // AND_Gate
  and and_7 (and_7_out, and_4_out, not_1_out);
  and and_8 (and_8_out, and_4_out, ~not_1_out);  // AND_Gate
  \mod60计数器  \mod60计数器_1  (
    .ADJ(1'b1), .CPU(and_1_out), .CPD(1'b0), .Q1D(out_14[3]), .Q1C(out_14[2]), .Q1B(out_14[1]),
    .Q1A(out_14[0]), .Q2D(out_13[3]), .Q2C(out_13[2]), .Q2B(out_13[1]), .Q2A(out_13[0]), .CLR(CLR),
    .out_13(\mod60计数器_1_out_13 ));
  // AND_Gate and_9 has open pins: in0=ADJ1, in1=ADJ0, out=open
  or or_1 (or_1_out, and_6_out, \mod60计数器_1_out_13 );
  or or_2 (or_2_out, and_3_out, and_10_out);
  and and_10 (and_10_out, ~ADJ0, or_1_out);  // AND_Gate
  \mod60计数器  \mod60计数器_2  (
    .ADJ(1'b1), .CPU(or_2_out), .CPD(and_8_out), .Q1D(out_12[3]), .Q1C(out_12[2]), .Q1B(out_12[1]),
    .Q1A(out_12[0]), .Q2D(out_10[3]), .Q2C(out_10[2]), .Q2B(out_10[1]), .Q2A(out_10[0]), .CLR(CLR),
    .out_13(\mod60计数器_2_out_13 ));
  or or_3 (or_3_out, and_5_out, \mod60计数器_2_out_13 );
  \mod12_24计数器  \mod12_24计数器_1  (
    .ADJ(1'b1), .CPU(or_3_out), .CPD(and_7_out), .SET(SET), .CLR(CLR), .QCC(\mod12_24计数器_1_qcc ),
    .out_7(out_9[0]), .out_8(out_9[1]), .out_9(out_9[2]), .out_10(out_9[3]), .out_11(out_8[0]),
    .out_12(out_8[1]), .out_13(out_8[2]), .out_14(out_8[3]));
  not not_2 (not_2_out, SET);
  T_Flip_Flop t_ff_1 (.clk(\mod12_24计数器_1_qcc ), .T(1'b1), .Q(t_ff_1_q), .reset(CLR));  // open: Qn, preset, en
  \整点报时电路  \u_整点报时电路_1  (.in_1(out_10), .in_2(out_12), .in_3(out_13), .out_5(\报时 ), .in_4(out_14));
  \LED电路  \led电路_1  (.out_3(out_15), .out_4(out_16), .out_5(out_17), .out_6(out_18), .AM_PM(t_ff_1_q), .TT(not_2_out));
endmodule

module \闹钟  (
  input  [3:0] \hour十位 ,
  input  [3:0] \闹钟hour十位 ,
  input  [3:0] \hour个位 ,
  input  [3:0] \闹钟hour个位 ,
  input  [3:0] \minute十位 ,
  input  [3:0] \闹钟minute十位 ,
  input  [3:0] \minute个位 ,
  input  [3:0] \闹钟minute个位 ,
  input  [3:0] \second十位 ,
  input  [4:0] \上下午 ,
  input  [4:0] \闹钟上下午 ,
  output \闹钟 
);

  wire comparator_1_eq, comparator_2_eq, comparator_3_eq, comparator_4_eq, comparator_5_eq, comparator_6_eq;

  Comparator #(.width(4), .mode("unsigned")) comparator_1 (
    .a(\hour十位 ), .b(\闹钟hour十位 ), .eq(comparator_1_eq));  // open: gt, lt
  Comparator #(.width(4), .mode("unsigned")) comparator_2 (
    .a(\hour个位 ), .b(\闹钟hour个位 ), .eq(comparator_2_eq));  // open: gt, lt
  Comparator #(.width(4), .mode("unsigned")) comparator_3 (
    .a(\minute十位 ), .b(\闹钟minute十位 ), .eq(comparator_3_eq));  // open: gt, lt
  Comparator #(.width(4), .mode("unsigned")) comparator_4 (
    .a(\minute个位 ), .b(\闹钟minute个位 ), .eq(comparator_4_eq));  // open: gt, lt
  Comparator #(.width(4), .mode("unsigned")) comparator_5 (
    .a(\second十位 ), .b(4'b0000), .eq(comparator_5_eq));  // open: gt, lt
  Comparator #(.width(5), .mode("unsigned")) comparator_6 (
    .a(\上下午 ), .b(\闹钟上下午 ), .eq(comparator_6_eq));  // open: gt, lt
  and and_1 (\闹钟 , comparator_1_eq, comparator_2_eq, comparator_3_eq, comparator_4_eq, comparator_5_eq, comparator_6_eq);
endmodule

module \电子钟_闹钟  (
  input  ADJ0,
  input  ALARM,
  input  ADJ1,
  input  in_4,
  input  in_5,
  input  in_6,
  input  in_7,
  input  in_8,
  output \报时 ,
  output [3:0] out_10,
  output [3:0] out_11,
  output [3:0] out_12,
  output [3:0] out_13,
  output \报时_2 ,
  output [3:0] out_15,
  output [3:0] out_16,
  output [4:0] out_17,
  output [4:0] out_18,
  output [4:0] out_19,
  output [4:0] out_20
);

  wire and_2_out, and_3_out, and_4_out, and_5_out, and_6_out, and_7_out, and_8_out, and_9_out, and_10_out,
       and_11_out, \电子钟_1_报时 ;
  wire [3:0] \电子钟_1_out_8 , \电子钟_1_out_9 , \电子钟_1_out_10 , \电子钟_1_out_12 , \电子钟_1_out_13 , \电子钟_1_out_14 ,
       \电子钟_2_out_8 , \电子钟_2_out_9 , \电子钟_2_out_10 , \电子钟_2_out_12 , \电子钟_2_out_13 , \电子钟_2_out_14 ;
  wire [4:0] \电子钟_1_out_15 , \电子钟_1_out_16 , \电子钟_1_out_17 , \电子钟_1_out_18 , \电子钟_2_out_15 , \电子钟_2_out_16 ,
       \电子钟_2_out_17 , \电子钟_2_out_18 ;

  // AND_Gate and_1 has open pins: in0=in_4, in1=ALARM, out=open
  and and_2 (and_2_out, in_4, ~ALARM);  // AND_Gate
  and and_3 (and_3_out, in_5, ALARM);
  and and_4 (and_4_out, in_5, ~ALARM);  // AND_Gate
  and and_5 (and_5_out, in_6, ALARM);
  and and_6 (and_6_out, in_6, ~ALARM);  // AND_Gate
  and and_7 (and_7_out, in_8, ALARM);
  and and_8 (and_8_out, in_8, ~ALARM);  // AND_Gate
  and and_9 (and_9_out, ALARM, ADJ1);
  and and_10 (and_10_out, ADJ0, ~ALARM);  // AND_Gate
  and and_11 (and_11_out, ADJ1, ~ALARM);  // AND_Gate
  \电子钟  \u_电子钟_1  (
    .CP(and_2_out), .ADJ0(and_10_out), .ADJ1(and_11_out), .CPU(and_4_out), .CPD(and_6_out), .CLR(and_8_out),
    .out_8(\电子钟_1_out_8 ), .out_9(\电子钟_1_out_9 ), .out_10(\电子钟_1_out_10 ), .out_12(\电子钟_1_out_12 ),
    .out_13(\电子钟_1_out_13 ), .out_14(\电子钟_1_out_14 ), .SET(in_7), .out_15(\电子钟_1_out_15 ),
    .out_16(\电子钟_1_out_16 ), .out_17(\电子钟_1_out_17 ), .out_18(\电子钟_1_out_18 ), .\报时 (\电子钟_1_报时 ));
  and and_12 (\报时_2 , \电子钟_1_报时 , ~ALARM);  // AND_Gate
  \电子钟  \u_电子钟_2  (
    .ADJ0(1'b1), .ADJ1(and_9_out), .CPU(and_3_out), .CPD(and_5_out), .CLR(and_7_out), .out_8(\电子钟_2_out_8 ),
    .out_9(\电子钟_2_out_9 ), .out_10(\电子钟_2_out_10 ), .out_12(\电子钟_2_out_12 ), .out_13(\电子钟_2_out_13 ),
    .out_14(\电子钟_2_out_14 ), .SET(in_7), .out_15(\电子钟_2_out_15 ), .out_16(\电子钟_2_out_16 ),
    .out_17(\电子钟_2_out_17 ), .out_18(\电子钟_2_out_18 ));  // open: CP, 报时
  \闹钟  \u_闹钟_1  (
    .\hour十位 (\电子钟_1_out_8 ), .\闹钟hour十位 (\电子钟_2_out_8 ), .\hour个位 (\电子钟_1_out_9 ),
    .\闹钟hour个位 (\电子钟_2_out_9 ), .\minute十位 (\电子钟_1_out_10 ), .\闹钟minute十位 (\电子钟_2_out_10 ),
    .\minute个位 (\电子钟_1_out_12 ), .\闹钟minute个位 (\电子钟_2_out_12 ), .\second十位 (\电子钟_1_out_13 ),
    .\上下午 (\电子钟_1_out_15 ), .\闹钟上下午 (\电子钟_2_out_15 ), .\闹钟 (\报时 ));
  Multiplexer #(.width(5), .enable("false")) multiplexer_1 (
    .in0(\电子钟_1_out_15 ), .in1(\电子钟_2_out_15 ), .out(out_17), .sel(ALARM));
  Multiplexer #(.width(5), .enable("false")) multiplexer_2 (
    .in0(\电子钟_1_out_16 ), .in1(\电子钟_2_out_16 ), .out(out_18), .sel(ALARM));
  Multiplexer #(.width(5), .enable("false")) multiplexer_3 (
    .in0(\电子钟_1_out_17 ), .in1(\电子钟_2_out_17 ), .out(out_19), .sel(ALARM));
  Multiplexer #(.width(5), .enable("false")) multiplexer_4 (
    .in0(\电子钟_1_out_18 ), .in1(\电子钟_2_out_18 ), .out(out_20), .sel(ALARM));
  Multiplexer #(.width(4), .enable("false")) multiplexer_5 (
    .in0(\电子钟_1_out_8 ), .in1(\电子钟_2_out_8 ), .out(out_10), .sel(ALARM));
  Multiplexer #(.width(4), .enable("false")) multiplexer_6 (
    .in0(\电子钟_1_out_9 ), .in1(\电子钟_2_out_9 ), .out(out_11), .sel(ALARM));
  Multiplexer #(.width(4), .enable("false")) multiplexer_7 (
    .in0(\电子钟_1_out_10 ), .in1(\电子钟_2_out_10 ), .out(out_12), .sel(ALARM));
  Multiplexer #(.width(4), .enable("false")) multiplexer_8 (
    .in0(\电子钟_1_out_12 ), .in1(\电子钟_2_out_12 ), .out(out_13), .sel(ALARM));
  Multiplexer #(.width(4), .enable("false")) multiplexer_9 (
    .in0(\电子钟_1_out_13 ), .in1(\电子钟_2_out_13 ), .out(out_15), .sel(ALARM));
  Multiplexer #(.width(4), .enable("false")) multiplexer_10 (
    .in0(\电子钟_1_out_14 ), .in1(\电子钟_2_out_14 ), .out(out_16), .sel(ALARM));
endmodule

module CESHI (
  input  in_1,
  input  in_2,
  input  in_3,
  input  in_4,
  input  in_5,
  input  in_6,
  input  in_7,
  input  in_8,
  input  in_9,
  input  in_10,
  input  in_11,
  input  [3:0] in_12,
  input  [3:0] in_13,
  input  [3:0] in_14,
  input  in_15,
  input  in_16,
  input  [3:0] in_17,
  input  [3:0] in_18,
  input  [3:0] in_19,
  input  [3:0] in_20,
  input  [3:0] in_21,
  input  [3:0] in_22,
  input  [3:0] in_23,
  input  [3:0] in_24,
  input  [3:0] in_25,
  input  [4:0] in_26,
  input  [4:0] in_27,
  output out_28,
  output out_29,
  output out_30
);

  wire button_1_out, button_2_out, button_3_out, button_4_out, button_5_out, button_6_out, button_7_out,
       button_8_out, clock_1_out, clock_2_out, \mod10计数器_1_cf , \整点报时电路_1_out_5 , \电子钟_闹钟_1_报时 ,
       \电子钟_闹钟_1_报时_2 , \闹钟_1_闹钟 ;
  wire [3:0] \mod10计数器_1_y1 , \mod12_24计数器_1_out_7 , \mod12_24计数器_1_out_11 , \mod60计数器_1_q1a ,
       \mod60计数器_1_q2a , \电子钟_闹钟_1_out_10 , \电子钟_闹钟_1_out_11 , \电子钟_闹钟_1_out_12 , \电子钟_闹钟_1_out_13 ,
       \电子钟_闹钟_1_out_15 , \电子钟_闹钟_1_out_16 ;
  wire [4:0] \led电路_1_out_3 , \led电路_1_out_4 , \led电路_1_out_5 , \led电路_1_out_6 , \电子钟_闹钟_1_out_17 ,
       \电子钟_闹钟_1_out_18 , \电子钟_闹钟_1_out_19 , \电子钟_闹钟_1_out_20 ;

  DotMatrix #(.matrixcols(4), .matrixrows(5)) dotmatrix_1 (
    .col0(\led电路_1_out_3 ), .col1(\led电路_1_out_4 ), .col2(\led电路_1_out_5 ), .col3(\led电路_1_out_6 ));
  \LED电路  \led电路_1  (
    .out_3(\led电路_1_out_3 ), .out_4(\led电路_1_out_4 ), .out_5(\led电路_1_out_5 ), .out_6(\led电路_1_out_6 ),
    .AM_PM(in_6), .TT(in_7));
  DotMatrix #(.matrixcols(4), .matrixrows(5)) dotmatrix_2 (
    .col0(\电子钟_闹钟_1_out_17 ), .col1(\电子钟_闹钟_1_out_18 ), .col2(\电子钟_闹钟_1_out_19 ), .col3(\电子钟_闹钟_1_out_20 ));
  Clock clock_1 (.out(clock_1_out));
  Button button_1 (.out(button_1_out));
  Button button_2 (.out(button_2_out));
  Clock clock_2 (.out(clock_2_out));
  Hex_Digit_Display hex_digit_display_1 (.value(\电子钟_闹钟_1_out_10 ));  // open: dp
  Button button_3 (.out(button_3_out));
  Hex_Digit_Display hex_digit_display_2 (.value(\mod10计数器_1_y1 ));  // open: dp
  \mod10计数器  \mod10计数器_1  (
    .CPU(button_1_out), .CPD(button_2_out), .Y1(\mod10计数器_1_y1 [0]), .Y2(\mod10计数器_1_y1 [1]),
    .Y3(\mod10计数器_1_y1 [2]), .Y4(\mod10计数器_1_y1 [3]), .CLR(in_8), .CF(\mod10计数器_1_cf ));
  \脉冲1HZ电路  \u_脉冲1hz电路_1  (.in_1(clock_2_out), .out_2(out_30));
  Hex_Digit_Display hex_digit_display_3 (.value(\电子钟_闹钟_1_out_12 ));  // open: dp
  Hex_Digit_Display hex_digit_display_4 (.value(\电子钟_闹钟_1_out_11 ));  // open: dp
  \电子钟_闹钟  \u_电子钟_闹钟_1  (
    .ADJ0(in_1), .ALARM(in_3), .ADJ1(in_2), .in_4(clock_1_out), .in_5(button_3_out), .in_6(button_4_out),
    .in_7(in_4), .in_8(in_5), .out_10(\电子钟_闹钟_1_out_10 ), .out_11(\电子钟_闹钟_1_out_11 ),
    .out_12(\电子钟_闹钟_1_out_12 ), .out_13(\电子钟_闹钟_1_out_13 ), .\报时_2 (\电子钟_闹钟_1_报时_2 ),
    .out_15(\电子钟_闹钟_1_out_15 ), .out_16(\电子钟_闹钟_1_out_16 ), .out_17(\电子钟_闹钟_1_out_17 ),
    .out_18(\电子钟_闹钟_1_out_18 ), .out_19(\电子钟_闹钟_1_out_19 ), .out_20(\电子钟_闹钟_1_out_20 ), .\报时 (\电子钟_闹钟_1_报时 ));
  Button button_4 (.out(button_4_out));
  \整点报时电路  \u_整点报时电路_1  (.in_1(in_12), .in_2(in_13), .in_3(in_14), .out_5(\整点报时电路_1_out_5 ));  // open: in_4
  \闹钟  \u_闹钟_1  (
    .\hour十位 (in_17), .\闹钟hour十位 (in_18), .\hour个位 (in_19), .\闹钟hour个位 (in_20), .\minute十位 (in_21),
    .\闹钟minute十位 (in_22), .\minute个位 (in_23), .\闹钟minute个位 (in_24), .\second十位 (in_25), .\上下午 (in_26),
    .\闹钟上下午 (in_27), .\闹钟 (\闹钟_1_闹钟 ));
  Hex_Digit_Display hex_digit_display_5 (.value(\电子钟_闹钟_1_out_13 ));  // open: dp
  LED led_1 (.in(\mod10计数器_1_cf ));
  LED led_2 (.in(\整点报时电路_1_out_5 ));
  LED led_3 (.in(\闹钟_1_闹钟 ));
  Hex_Digit_Display hex_digit_display_6 (.value(\电子钟_闹钟_1_out_15 ));  // open: dp
  Hex_Digit_Display hex_digit_display_7 (.value(\电子钟_闹钟_1_out_16 ));  // open: dp
  LED led_4 (.in(\电子钟_闹钟_1_报时 ));
  LED led_5 (.in(\电子钟_闹钟_1_报时_2 ));
  Button button_5 (.out(button_5_out));
  Button button_6 (.out(button_6_out));
  Button button_7 (.out(button_7_out));
  Button button_8 (.out(button_8_out));
  Hex_Digit_Display hex_digit_display_8 (.value(\mod12_24计数器_1_out_11 ));  // open: dp
  Hex_Digit_Display hex_digit_display_9 (.value(\mod60计数器_1_q2a ));  // open: dp
  \mod60计数器  \mod60计数器_1  (
    .ADJ(in_15), .CPU(button_7_out), .CPD(button_8_out), .Q1D(\mod60计数器_1_q1a [3]),
    .Q1C(\mod60计数器_1_q1a [2]), .Q1B(\mod60计数器_1_q1a [1]), .Q1A(\mod60计数器_1_q1a [0]),
    .Q2D(\mod60计数器_1_q2a [3]), .Q2C(\mod60计数器_1_q2a [2]), .Q2B(\mod60计数器_1_q2a [1]),
    .Q2A(\mod60计数器_1_q2a [0]), .CLR(in_16), .out_13(out_29));
  Hex_Digit_Display hex_digit_display_10 (.value(\mod12_24计数器_1_out_7 ));  // open: dp
  \mod12_24计数器  \mod12_24计数器_1  (
    .ADJ(in_9), .CPU(button_5_out), .CPD(button_6_out), .SET(in_10), .CLR(in_11), .QCC(out_28),
    .out_7(\mod12_24计数器_1_out_7 [0]), .out_8(\mod12_24计数器_1_out_7 [1]), .out_9(\mod12_24计数器_1_out_7 [2]),
    .out_10(\mod12_24计数器_1_out_7 [3]), .out_11(\mod12_24计数器_1_out_11 [0]),
    .out_12(\mod12_24计数器_1_out_11 [1]), .out_13(\mod12_24计数器_1_out_11 [2]), .out_14(\mod12_24计数器_1_out_11 [3]));
  Hex_Digit_Display hex_digit_display_11 (.value(\mod60计数器_1_q1a ));  // open: dp
endmodule

module temp (
  input  in_1,
  output out_2
);

  wire buffer_1_out, buffer_2_out, buffer_3_out, buffer_4_out, buffer_5_out, buffer_6_out, buffer_7_out,
       buffer_8_out;

  buf buffer_1 (buffer_1_out, buffer_2_out);
  buf buffer_2 (buffer_2_out, in_1);
  buf buffer_3 (buffer_3_out, buffer_1_out);
  buf buffer_4 (buffer_4_out, buffer_3_out);
  buf buffer_5 (buffer_5_out, buffer_4_out);
  buf buffer_6 (buffer_6_out, buffer_8_out);
  buf buffer_7 (buffer_7_out, buffer_6_out);
  buf buffer_8 (buffer_8_out, buffer_5_out);
  buf buffer_9 (out_2, buffer_7_out);
endmodule
