// Logisim project 4.circ as structural Verilog: 6 circuits, main circuit main
module sqrX (
  input  [31:0] a,
  input  [31:0] b,
  input  [31:0] c,
  input  [31:0] d,
  output [31:0] a_prime,
  output [31:0] b_prime,
  output [31:0] c_prime,
  output [31:0] d_prime
);

  wire [31:0] multiplier_1_out, multiplier_2_out, multiplier_3_out, multiplier_4_out, multiplier_5_out,
       multiplier_6_out, multiplier_7_out;

  Multiplier #(.width(32)) multiplier_1 (.a(a), .b(a), .out(multiplier_1_out));  // open: cin, cout
  Multiplier #(.width(32)) multiplier_2 (.a(a), .b(b), .out(multiplier_2_out));  // open: cin, cout
  Multiplier #(.width(32)) multiplier_3 (.a(a), .b(c), .out(multiplier_3_out));  // open: cin, cout
  Multiplier #(.width(32)) multiplier_4 (.a(b), .b(c), .out(multiplier_4_out));  // open: cin, cout
  Multiplier #(.width(32)) multiplier_5 (.a(b), .b(d), .out(multiplier_5_out));  // open: cin, cout
  Multiplier #(.width(32)) multiplier_6 (.a(c), .b(d), .out(multiplier_6_out));  // open: cin, cout
  Multiplier #(.width(32)) multiplier_7 (.a(d), .b(d), .out(multiplier_7_out));  // open: cin, cout
  Adder #(.width(32)) adder_1 (.a(multiplier_4_out), .b(multiplier_1_out), .out(a_prime));  // open: cin, cout
  Adder #(.width(32)) adder_2 (.a(multiplier_2_out), .b(multiplier_5_out), .out(b_prime));  // open: cin, cout
  Adder #(.width(32)) adder_3 (.a(multiplier_3_out), .b(multiplier_6_out), .out(c_prime));  // open: cin, cout
  Adder #(.width(32)) adder_4 (.a(multiplier_4_out), .b(multiplier_7_out), .out(d_prime));  // open: cin, cout
endmodule

module sqrX_A (
  input  [31:0] a,
  input  [31:0] b,
  input  [31:0] c,
  input  [31:0] d,
  output [31:0] a_prime_prime,
  output [31:0] b_prime_prime,
  output [31:0] c_prime_prime,
  output [31:0] d_prime_prime
);

  wire [31:0] adder_2_out, adder_4_out, multiplier_1_out, multiplier_2_out, multiplier_3_out,
       multiplier_4_out, multiplier_5_out, multiplier_6_out, multiplier_7_out;

  Multiplier #(.width(32)) multiplier_1 (.a(a), .b(a), .out(multiplier_1_out));  // open: cin, cout
  Multiplier #(.width(32)) multiplier_2 (.a(a), .b(b), .out(multiplier_2_out));  // open: cin, cout
  Multiplier #(.width(32)) multiplier_3 (.a(a), .b(c), .out(multiplier_3_out));  // open: cin, cout
  Multiplier #(.width(32)) multiplier_4 (.a(b), .b(c), .out(multiplier_4_out));  // open: cin, cout
  Multiplier #(.width(32)) multiplier_5 (.a(b), .b(d), .out(multiplier_5_out));  // open: cin, cout
  Multiplier #(.width(32)) multiplier_6 (.a(c), .b(d), .out(multiplier_6_out));  // open: cin, cout
  Multiplier #(.width(32)) multiplier_7 (.a(d), .b(d), .out(multiplier_7_out));  // open: cin, cout
  Adder #(.width(32)) adder_1 (.a(multiplier_2_out), .b(multiplier_5_out), .out(a_prime_prime));  // open: cin, cout
  Adder #(.width(32)) adder_2 (.a(multiplier_1_out), .b(multiplier_4_out), .out(adder_2_out));  // open: cin, cout
  Adder #(.width(32)) adder_3 (.a(multiplier_4_out), .b(multiplier_7_out), .out(c_prime_prime));  // open: cin, cout
  Adder #(.width(32)) adder_4 (.a(multiplier_3_out), .b(multiplier_6_out), .out(adder_4_out));  // open: cin, cout
  Adder #(.width(32)) adder_5 (.a(a_prime_prime), .b(adder_2_out), .out(b_prime_prime));  // open: cin, cout
  Adder #(.width(32)) adder_6 (.a(c_prime_prime), .b(adder_4_out), .out(d_prime_prime));  // open: cin, cout
endmodule

module Fibo (
  input  start,
  input  clr,
  input  Ni_1,
  input  clk,
  output [31:0] Fi
);

  wire [31:0] multiplexer_1_out, multiplexer_2_out, multiplexer_3_out, multiplexer_4_out, multiplexer_5_out,
       multiplexer_6_out, multiplexer_7_out, multiplexer_8_out, multiplexer_10_out, multiplexer_11_out,
       register_1_q, register_2_q, register_3_q, register_4_q, sqrx_1_a_prime, sqrx_1_b_prime,
       sqrx_1_c_prime, sqrx_1_d_prime, sqrx_a_1_a_prime_prime, sqrx_a_1_b_prime_prime,
       sqrx_a_1_c_prime_prime, sqrx_a_1_d_prime_prime;

  Multiplexer #(.width(32), .enable("false")) multiplexer_1 (
    .in0({32{1'b0}}), .in1(32'h1), .out(multiplexer_1_out), .sel(Ni_1));
  Multiplexer #(.width(32), .enable("false")) multiplexer_2 (
    .in0({32{1'b0}}), .in1(32'h1), .out(multiplexer_2_out), .sel(Ni_1));
  Multiplexer #(.width(32), .enable("false")) multiplexer_3 (
    .in0({32{1'b0}}), .in1(32'h1), .out(multiplexer_3_out), .sel(Ni_1));
  Multiplexer #(.width(32), .enable("false")) multiplexer_4 (
    .in0({32{1'b0}}), .in1(multiplexer_8_out), .out(multiplexer_4_out), .sel(start));
  Multiplexer #(.width(32), .enable("false")) multiplexer_5 (
    .in0(multiplexer_1_out), .in1(Fi), .out(multiplexer_5_out), .sel(start));
  Multiplexer #(.width(32), .enable("false")) multiplexer_6 (
    .in0(multiplexer_2_out), .in1(multiplexer_10_out), .out(multiplexer_6_out), .sel(start));
  Multiplexer #(.width(32), .enable("false")) multiplexer_7 (
    .in0(multiplexer_3_out), .in1(multiplexer_11_out), .out(multiplexer_7_out), .sel(start));
  Register #(.width(32), .trigger("falling")) register_1 (
    .D(multiplexer_4_out), .Q(register_1_q), .clk(clk), .clr(clr));  // open: en
  Register #(.width(32), .trigger("falling")) register_2 (
    .D(multiplexer_5_out), .Q(register_2_q), .clk(clk), .clr(clr));  // open: en
  Register #(.width(32), .trigger("falling")) register_3 (
    .D(multiplexer_6_out), .Q(register_3_q), .clk(clk), .clr(clr));  // open: en
  Register #(.width(32), .trigger("falling")) register_4 (
    .D(multiplexer_7_out), .Q(register_4_q), .clk(clk), .clr(clr));  // open: en
  sqrX sqrx_1 (
    .a(register_1_q), .b(register_2_q), .c(register_3_q), .d(register_4_q), .a_prime(sqrx_1_a_prime),
    .b_prime(sqrx_1_b_prime), .c_prime(sqrx_1_c_prime), .d_prime(sqrx_1_d_prime));
  sqrX_A sqrx_a_1 (
    .a(register_1_q), .b(register_2_q), .c(register_3_q), .d(register_4_q),
    .a_prime_prime(sqrx_a_1_a_prime_prime), .b_prime_prime(sqrx_a_1_b_prime_prime),
    .c_prime_prime(sqrx_a_1_c_prime_prime), .d_prime_prime(sqrx_a_1_d_prime_prime));
  Multiplexer #(.width(32), .enable("false")) multiplexer_8 (
    .in0(sqrx_1_a_prime), .in1(sqrx_a_1_a_prime_prime), .out(multiplexer_8_out), .sel(Ni_1));
  Multiplexer #(.width(32), .enable("false")) multiplexer_9 (
    .in0(sqrx_1_b_prime), .in1(sqrx_a_1_b_prime_prime), .out(Fi), .sel(Ni_1));
  Multiplexer #(.width(32), .enable("false")) multiplexer_10 (
    .in0(sqrx_1_c_prime), .in1(sqrx_a_1_c_prime_prime), .out(multiplexer_10_out), .sel(Ni_1));
  Multiplexer #(.width(32), .enable("false")) multiplexer_11 (
    .in0(sqrx_1_d_prime), .in1(sqrx_a_1_d_prime_prime), .out(multiplexer_11_out), .sel(Ni_1));
  // Probe on multiplexer_11_out
endmodule

module Display (
  input  [31:0] in_1,
  output [3:0] out_2,
  output [3:0] out_3,
  output [3:0] out_4,
  output [3:0] out_5,
  output [3:0] out_6,
  output [3:0] out_7,
  output [3:0] out_8,
  output [3:0] out_9,
  output [3:0] out_10,
  output [3:0] out_11
);

  wire [31:0] divider_1_out, divider_2_out, divider_3_out, divider_4_out, divider_5_out, divider_6_out,
       divider_7_out, divider_8_out, divider_9_out;
  wire [31:4] divider_1_rem, divider_2_rem, divider_3_rem, divider_4_rem, divider_5_rem, divider_6_rem,
       divider_7_rem, divider_8_rem, divider_9_rem, divider_10_rem;

  Divider #(.width(32)) divider_1 (
    .a(in_1), .b(32'ha), .out(divider_1_out), .rem({divider_1_rem, out_2}));  // open: upper
  Divider #(.width(32)) divider_2 (
    .a(divider_1_out), .b(32'ha), .out(divider_2_out), .rem({divider_2_rem, out_3}));  // open: upper
  Divider #(.width(32)) divider_3 (
    .a(divider_2_out), .b(32'ha), .out(divider_3_out), .rem({divider_3_rem, out_4}));  // open: upper
  Divider #(.width(32)) divider_4 (
    .a(divider_3_out), .b(32'ha), .out(divider_4_out), .rem({divider_4_rem, out_5}));  // open: upper
  Divider #(.width(32)) divider_5 (
    .a(divider_4_out), .b(32'ha), .out(divider_5_out), .rem({divider_5_rem, out_6}));  // open: upper
  Divider #(.width(32)) divider_6 (
    .a(divider_5_out), .b(32'ha), .out(divider_6_out), .rem({divider_6_rem, out_7}));  // open: upper
  Divider #(.width(32)) divider_7 (
    .a(divider_6_out), .b(32'ha), .out(divider_7_out), .rem({divider_7_rem, out_8}));  // open: upper
  Divider #(.width(32)) divider_8 (
    .a(divider_7_out), .b(32'ha), .out(divider_8_out), .rem({divider_8_rem, out_9}));  // open: upper
  Divider #(.width(32)) divider_9 (
    .a(divider_8_out), .b(32'ha), .out(divider_9_out), .rem({divider_9_rem, out_10}));  // open: upper
  Divider #(.width(32)) divider_10 (.a(divider_9_out), .b(32'ha), .rem({divider_10_rem, out_11}));  // open: out, upper
endmodule

module main (
  input  clear,
  input  clock,
  input  [5:0] n,
  output [3:0] out_4,
  output [3:0] out_5,
  output [3:0] out_6,
  output [3:0] out_7,
  output [3:0] out_8,
  output [3:0] out_9,
  output [3:0] out_10,
  output [3:0] out_11,
  output [3:0] out_12,
  output [3:0] out_13
);

  wire and_1_out, and_2_out, buffer_1_out, buffer_2_out, buffer_3_out, buffer_4_out, comparator_1_eq,
       comparator_1_gt, d_ff_1_q, not_1_out, or_1_out, or_2_out, or_3_out, or_4_out, shift_register_1_out;
  wire [7:0] counter_1_q;
  wire [31:0] fibo_1_fi;

  buf buffer_1 (buffer_1_out, clear);
  buf buffer_2 (buffer_2_out, buffer_1_out);
  buf buffer_3 (buffer_3_out, buffer_4_out);
  buf buffer_4 (buffer_4_out, not_1_out);
  not not_1 (not_1_out, clear);
  Shift_Register #(.length(6), .trigger("falling")) shift_register_1 (
    .shift(buffer_3_out), .in(1'b0), .clk(or_1_out), .out(shift_register_1_out), .load(buffer_2_out),
    .d0(n[0]), .d1(n[1]), .d2(n[2]), .d3(n[3]), .d4(n[4]), .d5(n[5]));  // open: clr, q0, q1, q2, q3, q4, q5
  or or_1 (or_1_out, clock, clear);
  Counter #(.ongoal("stay"), .trigger("falling")) counter_1 (
    .count(1'b1), .Q(counter_1_q), .clk(clock), .clr(clear));  // open: load, D, carry
  and and_1 (and_1_out, n[0], comparator_1_gt);
  or or_2 (or_2_out, comparator_1_gt, comparator_1_eq);
  Comparator #(.mode("unsigned")) comparator_1 (
    .a(counter_1_q), .b(8'h5), .gt(comparator_1_gt), .eq(comparator_1_eq));  // open: lt
  or or_3 (or_3_out, shift_register_1_out, d_ff_1_q);
  or or_4 (or_4_out, shift_register_1_out, and_1_out);
  and and_2 (and_2_out, clock, ~or_2_out);  // AND_Gate
  D_Flip_Flop #(.trigger("falling")) d_ff_1 (
    .clk(clock), .D(or_3_out), .Q(d_ff_1_q), .reset(clear));  // open: Qn, preset, en
  Fibo fibo_1 (.start(d_ff_1_q), .clr(clear), .Ni_1(or_4_out), .clk(and_2_out), .Fi(fibo_1_fi));
  Display display_1 (
    .in_1(fibo_1_fi), .out_2(out_13), .out_3(out_12), .out_4(out_11), .out_5(out_10), .out_6(out_9),
    .out_7(out_8), .out_8(out_7), .out_9(out_6), .out_10(out_5), .out_11(out_4));
endmodule

module Test (
  input  [5:0] in_1
);

  wire button_1_out, button_2_out;
  wire [3:0] main_1_out_4, main_1_out_5, main_1_out_6, main_1_out_7, main_1_out_8, main_1_out_9,
       main_1_out_10, main_1_out_11, main_1_out_12, main_1_out_13;

  Button button_1 (.out(button_1_out));
  Button button_2 (.out(button_2_out));
  Hex_Digit_Display hex_digit_display_1 (.value(main_1_out_5));  // open: dp
  Hex_Digit_Display hex_digit_display_2 (.value(main_1_out_4));  // open: dp
  Hex_Digit_Display hex_digit_display_3 (.value(main_1_out_6));  // open: dp
  Hex_Digit_Display hex_digit_display_4 (.value(main_1_out_7));  // open: dp
  main main_1 (
    .clear(button_1_out), .clock(button_2_out), .n(in_1), .out_4(main_1_out_4), .out_5(main_1_out_5),
    .out_6(main_1_out_6), .out_7(main_1_out_7), .out_8(main_1_out_8), .out_9(main_1_out_9),
    .out_10(main_1_out_10), .out_11(main_1_out_11), .out_12(main_1_out_12), .out_13(main_1_out_13));
  Hex_Digit_Display hex_digit_display_5 (.value(main_1_out_9));  // open: dp
  Hex_Digit_Display hex_digit_display_6 (.value(main_1_out_8));  // open: dp
  Hex_Digit_Display hex_digit_display_7 (.value(main_1_out_11));  // open: dp
  Hex_Digit_Display hex_digit_display_8 (.value(main_1_out_10));  // open: dp
  Hex_Digit_Display hex_digit_display_9 (.value(main_1_out_13));  // open: dp
  Hex_Digit_Display hex_digit_display_10 (.value(main_1_out_12));  // open: dp
endmodule
