// Logisim project Chap3_2_带时钟控制的R-S触发器.circ as structural Verilog: 1 circuit, main circuit main
module main (
  input  \初始化信号 ,
  input  R,
  input  S,
  output nQ,
  output Q
);

  wire Cp_out, nand_2_out, nand_4_out;

  nand nand_1 (nQ, nand_2_out, \初始化信号 , Q);
  nand nand_2 (nand_2_out, R, Cp_out);
  Button Cp (.out(Cp_out));
  nand nand_3 (Q, nQ, nand_4_out);
  nand nand_4 (nand_4_out, Cp_out, S);

  // Notes on the sheet:
  //   G1
  //   G3
  //   输入变量R,S,Cp
  //   输出变量/Q,Q
  //   带时钟控制的R-S触发器（与非门）
  //   G2
  //   G4
  //   仿真出现问题，重置模拟器，然后再重启
  //   功能表
  //   R     S         Qn+1
  //   0     0            Q
  //   0      1           1
  //   1      0           0
  //   1       1           d
  //   电路表现为.。。。.
endmodule
