// Logisim project Chap3_3_钟控JK触发器 .circ as structural Verilog: 2 circuits, main circuit main
module main (
  input  \启动开关 ,
  input  K,
  input  J,
  output nQ,
  output Q
);

  wire Cp_out, nand_2_out, nand_4_out;

  nand nand_1 (nQ, nand_2_out, \启动开关 , Q);
  nand nand_2 (nand_2_out, Q, K, Cp_out);
  Button Cp (.out(Cp_out));
  nand nand_3 (Q, nQ, nand_4_out);
  nand nand_4 (nand_4_out, Cp_out, J, nQ);

  // Notes on the sheet:
  //   操作步骤
  //   1、将启动开关至为1，无效状态。
  //   G1
  //   G3
  //   2、设置J，K的值，并将CP由0变为1再变为0；
  //   注意：启动开关的目的是确保状态有值，初值为0，至为1时开关无效。
  //   钟控JK触发器
  //   输出变量/Q,Q
  //   输入变量J,K,Cp
  //   3、J=K=1时，电路有震荡，可以点击模拟菜单中的启用信号模拟功能（或用Ctrl+E），确认状态输出。
  //   G2
  //   G4
  //   J     K         Qn+1
  //   0     0            Q
  //   0      1           0
  //   1      0           1
  //   1       1           /Q
  //   功能表
endmodule

module \带时钟R_S触发器封装  (
  input  R,
  input  S,
  output nQ,
  output Q
);

  wire Cp_out;

  main \u_带时钟R_S触发器  (.nQ(nQ), .Q(Q), .K(R), .J(S));  // open: 启动开关
  Button Cp (.out(Cp_out));
endmodule
