// Logisim project Chap4_3_逻辑判断.circ as structural Verilog: 1 circuit, main circuit 逻辑判断
module \逻辑判断  (
  input  a,
  input  b,
  input  c,
  input  d,
  input  a_2,
  input  b_2,
  input  c_2,
  input  d_2,
  output f,
  output f_2
);

  wire and_1_out, and_2_out, and_3_out, and_4_out, not_1_out, or_1_out, or_2_out;

  and and_1 (and_1_out, a, b);
  and and_2 (and_2_out, a_2, b_2);
  not not_1 (not_1_out, b_2);
  or or_1 (or_1_out, and_1_out, c);
  and and_3 (and_3_out, a, d);
  or or_2 (or_2_out, and_2_out, c_2);
  and and_4 (and_4_out, a_2, not_1_out, d_2);
  nor nor_1 (f, or_1_out, and_3_out);
  nor nor_2 (f_2, or_2_out, and_4_out);

  // Notes on the sheet:
  //   输入变量a，b，c，d
  //   输入变量a，b，c，d
  //   F  = /(AB+C+AD)   
  //   F=/（AB+C+A/BD)    
  //   输出变量F
  //   输出变量F
endmodule
