// Logisim project Chap4_5_1位全加器.circ as structural Verilog: 2 circuits, main circuit main
module main (
  input  A,
  input  B,
  input  Ci,
  output Si,
  output Ci_2
);

  wire \与非_2_out , \与非_3_out , \与非_out , \异或_out ;

  xor \u_异或  (\异或_out , A, B);
  nand \u_与非  (\与非_out , Ci, B);
  nand \u_与非_2  (\与非_2_out , Ci, A);
  nand \u_与非_3  (\与非_3_out , B, A);
  xor \u_异或_2  (Si, \异或_out , Ci);
  nand \u_与非_4  (Ci_2, \与非_out , \与非_2_out , \与非_3_out );
endmodule

// 加法器
module Adder (
  input  A,
  input  B,
  input  Ci,
  output Si,
  output Ci_1
);

  main adder (.A(Ci), .B(B), .Ci(A), .Si(Ci_1), .Ci_2(Si));
  LED led_1 (.in(Si));
  LED led_2 (.in(Ci_1));
endmodule
