// Logisim project Chap5_1_可逆计数器.circ as structural Verilog: 1 circuit, main circuit 2位二进制可逆计数器
module \_2位二进制可逆计数器  (
  input  X,
  input  \置1 ,
  input  \置0 ,
  output Y2,
  output Y1
);

  wire Cp_out, xnor_1_out;

  Button Cp (.out(Cp_out));
  xnor xnor_1 (xnor_1_out, X, Y1);
  J_K_Flip_Flop K2 (.J(xnor_1_out), .clk(Cp_out), .K(xnor_1_out), .Q(Y2), .preset(\置1 ), .reset(\置0 ));  // open: Qn, en
  J_K_Flip_Flop K1 (.J(1'b1), .clk(Cp_out), .K(1'b1), .Q(Y1), .preset(\置1 ), .reset(\置0 ));  // open: Qn, en
  LED led_1 (.in(Y2));
  LED led_2 (.in(Y1));

  // Notes on the sheet:
  //   2位二进制可逆计数器
endmodule
