// Logisim project Chap5_3_串行奇偶检测器.circ as structural Verilog: 1 circuit, main circuit main
module main (
  input  Enabe,
  input  x,
  output Z
);

  wire and_1_out, and_2_out, Cp_out, D1_q, D2_q, D3_q, D3_qn, nor_1_out, or_1_out, xor_1_out, xor_2_out;

  Button Cp (.out(Cp_out));
  and and_1 (and_1_out, D3_qn, x);
  xor xor_1 (xor_1_out, D3_q, x);
  or or_1 (or_1_out, and_1_out, D2_q);
  nor nor_1 (nor_1_out, D2_q, D3_q);
  and and_2 (and_2_out, D2_q, xor_1_out);
  D_Flip_Flop D3 (.clk(Cp_out), .D(or_1_out), .Q(D3_q), .Qn(D3_qn), .en(Enabe));  // open: preset, reset
  D_Flip_Flop D2 (.clk(Cp_out), .D(nor_1_out), .Q(D2_q), .en(Enabe));  // open: Qn, preset, reset
  D_Flip_Flop D1 (.clk(Cp_out), .D(and_2_out), .Q(D1_q), .en(Enabe));  // open: Qn, preset, reset
  LED Y3 (.in(D3_q));
  LED Y2 (.in(D2_q));
  LED Y1 (.in(D1_q));
  xor xor_2 (xor_2_out, D1_q, x);
  nor nor_2 (Z, D3_qn, D2_q, xor_2_out);

  // Notes on the sheet:
  //   3位二进制串行码偶检测器
  //   注意：输入1-0-1时，输出时刻
  //   输入0-1-1时，输出时刻
endmodule
