// Logisim project Chap6_3_异步电平分析.circ as structural Verilog: 1 circuit, main circuit 电平异步分析
module \电平异步分析  (
  input  X2,
  input  X1,
  output Z,
  output Y2,
  output Y1
);

  wire and_2_out, and_3_out, and_4_out, not_1_out, not_2_out;

  and and_1 (Z, Y1, Y2);
  and and_2 (and_2_out, Y2, X1, X2);
  or or_1 (Y2, and_2_out, and_3_out);
  and and_3 (and_3_out, X2, not_1_out, not_2_out);
  not not_1 (not_1_out, X1);
  not not_2 (not_2_out, Y1);
  or or_2 (Y1, and_4_out, X1);
  and and_4 (and_4_out, Y1, X2);

  // Notes on the sheet:
  //   状态y2
  //   X2X1输入序列：00-01-11-10-00-10-11-01
  //   状态y1
endmodule
