// Logisim project chap4_1_多数表决电路.circ as structural Verilog: 1 circuit, main circuit chap4_表决电路
module \chap4_表决电路  (
  input  A,
  input  B,
  input  C,
  output F
);

  wire nand_1_out, nand_2_out, nand_3_out;

  nand nand_1 (nand_1_out, A, B);
  nand nand_2 (nand_2_out, B, C);
  nand nand_3 (nand_3_out, C, A);
  nand nand_4 (F, nand_1_out, nand_2_out, nand_3_out);

  // Notes on the sheet:
  //   输入信号
  //   表决电路
  //   输出信号
endmodule
