// Logisim project chap4_4_合数判断(余3码).circ as structural Verilog: 1 circuit, main circuit chap4_合数判断(余3码)
module \chap4_合数判断_余3码  (
  input  A,
  input  B,
  input  C,
  input  D,
  output F
);

  wire nand_1_out, nand_2_out, nand_3_out;

  nand nand_1 (nand_1_out, A, B);
  nand nand_2 (nand_2_out, A, D);
  nand nand_3 (nand_3_out, B, C, D);
  nand nand_4 (F, nand_1_out, nand_2_out, nand_3_out);

  // Notes on the sheet:
  //   输入信号
  //   考虑了无关项m13（1101），m14（1110），m15（1111）
  //   组合判别以余3码表示的1 位十进制数是否为合数4,6,8,9
  //   F=AB+AD+BCD
  //   输出信号
endmodule
