// Logisim project chap5_2_同步101序列检测器.circ as structural Verilog: 1 circuit, main circuit main
module main (
  input  x,
  output Z
);

  wire and_1_out, Cp_out, not_1_out, xor_1_out, Y1_q, Y2_q;

  not not_1 (not_1_out, x);
  and and_1 (and_1_out, Y1_q, not_1_out);
  xor xor_1 (xor_1_out, Y1_q, not_1_out);
  Button Cp (.out(Cp_out));
  LED \u_观察点  (.in(Y1_q));
  J_K_Flip_Flop Y1 (.J(x), .clk(Cp_out), .K(not_1_out), .Q(Y1_q));  // open: Qn, preset, en, reset
  J_K_Flip_Flop Y2 (.J(and_1_out), .clk(Cp_out), .K(xor_1_out), .Q(Y2_q));  // open: Qn, preset, en, reset
  LED \u_观察点_2  (.in(Y2_q));
  and and_2 (Z, Y1_q, Y2_q);

  // Notes on the sheet:
  //   输入信号
  //   用J-K触发器设计的“101”序列检测器
  //   输出信号
endmodule
